// Logisim project Anzeige_7Segment.circ as structural Verilog: 17 circuits, main circuit Hauptschaltung_7Seg_Anzeige
module Hauptschaltung_7Seg_Anzeige (
  input  Takt_Wecker_Stellen,
  input  Taste_Gecko_Min_Sek,
  input  Taste_Gecko_Tag_Mon,
  input  Taste_Gecko_Jahr,
  input  Schalter_Gecko_Wecker_Stellem,
  input  [4:0] Tagbits,
  input  [4:0] Stundenbits,
  input  [4:0] Wecker_Stundenbits,
  input  [3:0] Monatbits,
  input  [5:0] Minutenbits,
  input  [5:0] Wecker_Minutenbits,
  input  [6:0] Jahrbits,
  input  [5:0] Sekundenbits,
  input  Schalter_Gecko_Wecker_Ein_Aus,
  output Seg_1A,
  output Seg_1B,
  output Seg_1C,
  output Seg_1D,
  output Seg_1E,
  output Seg_1F,
  output Seg_1G,
  output Seg_2A,
  output Seg_2B,
  output Seg_2C,
  output Seg_2D,
  output Seg_2E,
  output Seg_2F,
  output Seg_2G,
  output Seg_3A,
  output Seg_3B,
  output Seg_3C,
  output Seg_3D,
  output Seg_3E,
  output Seg_3F,
  output Seg_3G,
  output Seg_4A,
  output Seg_4B,
  output Seg_4C,
  output Seg_4D,
  output Seg_4E,
  output Seg_4F,
  output Seg_4G,
  output Reset_Wecker_Seg1,
  output Reset_Wecker_Seg3_4,
  output Reset_Wecker_Seg2,
  output Weckerfunktion_zu_LED,
  output Min_sek_zu_LED,
  output Tag_Mon_zu_LED,
  output Jahr_zu_LED
);

  wire bcd7seg2_seg_a, bcd7seg2_seg_b, bcd7seg2_seg_c, bcd7seg2_seg_d, bcd7seg2_seg_e, bcd7seg2_seg_f,
       bcd7seg2_seg_g, bcd7seg3_seg_a, bcd7seg3_seg_b, bcd7seg3_seg_c, bcd7seg3_seg_d, bcd7seg3_seg_e,
       bcd7seg3_seg_f, bcd7seg3_seg_g, bcd7seg_1_seg_a, bcd7seg_1_seg_b, bcd7seg_1_seg_c, bcd7seg_1_seg_d,
       bcd7seg_1_seg_e, bcd7seg_1_seg_f, bcd7seg_1_seg_g, bcd7seg_seg_a, bcd7seg_seg_b, bcd7seg_seg_c,
       bcd7seg_seg_d, bcd7seg_seg_e, bcd7seg_seg_f, bcd7seg_seg_g, binbcd2_d_0, binbcd2_d_1, binbcd2_d_2,
       binbcd2_d_3, binbcd2_u_0, binbcd2_u_1, binbcd2_u_2, binbcd2_u_3, binbcd_d_0, binbcd_d_1, binbcd_d_2,
       binbcd_d_3, binbcd_u_0, binbcd_u_1, binbcd_u_2, binbcd_u_3, minmony2_a, minmony2_a_1, minmony2_a_2,
       minmony2_a_3, minmony2_a_4, minmony2_a_5, minmony_a, minmony_a_1, minmony_a_2, minmony_a_3,
       minmony_a_4, minmony_a_5, multiplxmin_mon_bit0, multiplxmin_mon_bit1, multiplxmin_mon_bit2,
       multiplxmin_mon_bit3, multiplxmin_mon_bit4, multiplxmin_mon_bit5, multiplxstd_d_bit0,
       multiplxstd_d_bit1, multiplxstd_d_bit2, multiplxstd_d_bit3, multiplxstd_d_bit4, multiplxy_s_bit0,
       multiplxy_s_bit1, multiplxy_s_bit2, multiplxy_s_bit3, multiplxy_s_bit4, multiplxy_s_bit5,
       multiplxy_s_bit6, Rst_wecker_Seg2_reset_seg2, rstwecker1_rsseg1, rstwecker2_rsseg3,
       tstnfehler_wecker_stellen, umschaltng_seg1_bit_0, umschaltng_seg1_bit_1, umschaltng_seg1_bit_2,
       umschaltng_seg1_bit_3, umschaltng_seg1_bit_4, umschaltng_seg1_bit_5, umschaltng_seg2_bit_0,
       umschaltng_seg2_bit_1, umschaltng_seg2_bit_2, umschaltng_seg2_bit_3, umschaltng_seg2_bit_4,
       umschaltng_seg2_bit_5;

  Tastenfehler tstnfehler (
    .Taste_Gecko_Min_Sek(Taste_Gecko_Min_Sek), .Taste_Gecko_Tag_Mon(Taste_Gecko_Tag_Mon),
    .Taste_Gecko_Jahr(Taste_Gecko_Jahr), .Schalter_Gecko_Wecker_Stellen(Schalter_Gecko_Wecker_Stellem),
    .Taste_Min_Sek(Min_sek_zu_LED), .Taste_Tag_Mon(Tag_Mon_zu_LED), .Taste_Jahr(Jahr_zu_LED),
    .Wecker_Stellen(tstnfehler_wecker_stellen));
  Multiplex_Std_Tag multiplxstd_d (
    .Eingangstaste_Min_Sek(Min_sek_zu_LED), .Eingangstaste_Tag_Monat(Tag_Mon_zu_LED),
    .Eingangstaste_Jahr(Jahr_zu_LED), .Wecker_Stellen(tstnfehler_wecker_stellen), .Tag_Bit0(Tagbits[0]),
    .Tag_Bit1(Tagbits[1]), .Tag_Bit2(Tagbits[2]), .Tag_Bit3(Tagbits[3]), .Tag_Bit4(Tagbits[4]),
    .Std_Bit0(Stundenbits[0]), .Std_Bit1(Stundenbits[1]), .Std_Bit2(Stundenbits[2]),
    .Std_Bit3(Stundenbits[3]), .Std_Bit4(Stundenbits[4]), .Wecker_Std_Bit_0(Wecker_Stundenbits[0]),
    .Wecker_Std_Bit_1(Wecker_Stundenbits[1]), .Wecker_Std_Bit_2(Wecker_Stundenbits[2]),
    .Wecker_Std_Bit_3(Wecker_Stundenbits[3]), .Wecker_Std_Bit_4(Wecker_Stundenbits[4]),
    .Bit0(multiplxstd_d_bit0), .Bit1(multiplxstd_d_bit1), .Bit2(multiplxstd_d_bit2),
    .Bit3(multiplxstd_d_bit3), .Bit4(multiplxstd_d_bit4));
  Multiplex_Min_Monat multiplxmin_mon (
    .Eingangstaste_Tag_Monat(Tag_Mon_zu_LED), .Eingangstaste_Jahr(Jahr_zu_LED),
    .Wecker_Stellen(tstnfehler_wecker_stellen), .Monat_Bit0(Monatbits[0]), .Monat_Bit1(Monatbits[1]),
    .Monat_Bit2(Monatbits[2]), .Monat_Bit3(Monatbits[3]), .Min_Bit0(Minutenbits[0]),
    .Min_Bit1(Minutenbits[1]), .Min_Bit2(Minutenbits[2]), .Min_Bit3(Minutenbits[3]),
    .Min_Bit4(Minutenbits[4]), .Min_Bit5(Minutenbits[5]), .Wecker_Min_Bit_0(Wecker_Minutenbits[0]),
    .Wecker_Min_Bit_1(Wecker_Minutenbits[1]), .Wecker_Min_Bit_2(Wecker_Minutenbits[2]),
    .Wecker_Min_Bit_3(Wecker_Minutenbits[3]), .Wecker_Min_Bit_4(Wecker_Minutenbits[4]),
    .Wecker_Min_Bit_5(Wecker_Minutenbits[5]), .Bit0(multiplxmin_mon_bit0), .Bit1(multiplxmin_mon_bit1),
    .Bit2(multiplxmin_mon_bit2), .Bit3(multiplxmin_mon_bit3), .Bit4(multiplxmin_mon_bit4),
    .Bit5(multiplxmin_mon_bit5));
  Multiplex_Jahr_Sekunden multiplxy_s (
    .Eingangstaste_Jahr(Jahr_zu_LED), .Eingangstaste_Min_Sek(Min_sek_zu_LED), .Jahr_Bit0(Jahrbits[0]),
    .Jahr_Bit1(Jahrbits[1]), .Jahr_Bit2(Jahrbits[2]), .Jahr_Bit3(Jahrbits[3]), .Jahr_Bit4(Jahrbits[4]),
    .Jahr_Bit5(Jahrbits[5]), .Jahr_Bit6(Jahrbits[6]), .Sekunden_Bit_0(Sekundenbits[0]),
    .Sekunden_Bit_1(Sekundenbits[1]), .Sekunden_Bit_2(Sekundenbits[2]), .Sekunden_Bit_3(Sekundenbits[3]),
    .Sekunden_Bit_4(Sekundenbits[4]), .Sekunden_Bit_5(Sekundenbits[5]), .Bit0(multiplxy_s_bit0),
    .Bit1(multiplxy_s_bit1), .Bit2(multiplxy_s_bit2), .Bit3(multiplxy_s_bit3), .Bit4(multiplxy_s_bit4),
    .Bit5(multiplxy_s_bit5), .Bit6(multiplxy_s_bit6));
  Weckfunktion_Zeitvergleich weck_zeitvergl (
    .Wecker_Ein_Aus(Schalter_Gecko_Wecker_Ein_Aus), .Stunde_Aktuell_0(Stundenbits[0]),
    .Stunde_Aktuell_1(Stundenbits[1]), .Stunde_Aktuell_2(Stundenbits[2]), .Stunde_Aktuell_3(Stundenbits[3]),
    .Stunde_Aktuell_4(Stundenbits[4]), .Stunde_Wecker_0(Wecker_Stundenbits[0]),
    .Stunde_Wecker_1(Wecker_Stundenbits[1]), .Stunde_Wecker_2(Wecker_Stundenbits[2]),
    .Stunde_Wecker_3(Wecker_Stundenbits[3]), .Stunde_Wecker_4(Wecker_Stundenbits[4]),
    .MInute_Aktuell_0(Minutenbits[0]), .MInute_Aktuell_1(Minutenbits[1]), .MInute_Aktuell_2(Minutenbits[2]),
    .MInute_Aktuell_3(Minutenbits[3]), .MInute_Aktuell_4(Minutenbits[4]), .MInute_Aktuell_5(Minutenbits[5]),
    .MInute_Wecker_0(Wecker_Minutenbits[0]), .MInute_Wecker_1(Wecker_Minutenbits[1]),
    .MInute_Wecker_2(Wecker_Minutenbits[2]), .MInute_Wecker_3(Wecker_Minutenbits[3]),
    .MInute_Wecker_4(Wecker_Minutenbits[4]), .MInute_Wecker_5(Wecker_Minutenbits[5]),
    .Nach_LED_Anzeige_Weckfunktion(Weckerfunktion_zu_LED));
  Umschaltung_Min umschaltng (
    .Taste_Min_Sek(Min_sek_zu_LED), .Bit_0(multiplxmin_mon_bit0), .Bit_1(multiplxmin_mon_bit1),
    .Bit_2(multiplxmin_mon_bit2), .Bit_3(multiplxmin_mon_bit3), .Bit_4(multiplxmin_mon_bit4),
    .Bit_5(multiplxmin_mon_bit5), .Seg1_Bit_0(umschaltng_seg1_bit_0), .Seg1_Bit_1(umschaltng_seg1_bit_1),
    .Seg1_Bit_2(umschaltng_seg1_bit_2), .Seg1_Bit_3(umschaltng_seg1_bit_3),
    .Seg1_Bit_4(umschaltng_seg1_bit_4), .Seg1_Bit_5(umschaltng_seg1_bit_5),
    .Seg2_Bit_0(umschaltng_seg2_bit_0), .Seg2_Bit_1(umschaltng_seg2_bit_1),
    .Seg2_Bit_2(umschaltng_seg2_bit_2), .Seg2_Bit_3(umschaltng_seg2_bit_3),
    .Seg2_Bit_4(umschaltng_seg2_bit_4), .Seg2_Bit_5(umschaltng_seg2_bit_5));
  Verknuepfung_min_mon_jahr minmony (
    .e(multiplxstd_d_bit0), .e_1(umschaltng_seg1_bit_0), .e_2(multiplxstd_d_bit1),
    .e_3(umschaltng_seg1_bit_1), .e_4(multiplxstd_d_bit2), .e_5(umschaltng_seg1_bit_2),
    .e_6(multiplxstd_d_bit3), .e_7(umschaltng_seg1_bit_3), .e_8(multiplxstd_d_bit4),
    .e_9(umschaltng_seg1_bit_4), .e_10(1'b0), .e_11(umschaltng_seg1_bit_5), .a(minmony_a), .a_1(minmony_a_1),
    .a_2(minmony_a_2), .a_3(minmony_a_3), .a_4(minmony_a_4), .a_5(minmony_a_5));
  Bin2_BCD binbcd (
    .A_0(minmony_a), .A_1(minmony_a_1), .A_2(minmony_a_2), .A_3(minmony_a_3), .A_4(minmony_a_4),
    .A_5(minmony_a_5), .D_0(binbcd_d_0), .D_1(binbcd_d_1), .D_2(binbcd_d_2), .D_3(binbcd_d_3),
    .U_0(binbcd_u_0), .U_1(binbcd_u_1), .U_2(binbcd_u_2), .U_3(binbcd_u_3));  // open: A_6, A_7, A_8, C_0, C_1, C_2
  Verknuepfung_min_mon_jahr minmony2 (
    .e(umschaltng_seg2_bit_0), .e_1(multiplxy_s_bit0), .e_2(umschaltng_seg2_bit_1), .e_3(multiplxy_s_bit1),
    .e_4(umschaltng_seg2_bit_2), .e_5(multiplxy_s_bit2), .e_6(umschaltng_seg2_bit_3), .e_7(multiplxy_s_bit3),
    .e_8(umschaltng_seg2_bit_4), .e_9(multiplxy_s_bit4), .e_10(umschaltng_seg2_bit_5),
    .e_11(multiplxy_s_bit5), .a(minmony2_a), .a_1(minmony2_a_1), .a_2(minmony2_a_2), .a_3(minmony2_a_3),
    .a_4(minmony2_a_4), .a_5(minmony2_a_5));
  Bin2_BCD binbcd2 (
    .A_0(minmony2_a), .A_1(minmony2_a_1), .A_2(minmony2_a_2), .A_3(minmony2_a_3), .A_4(minmony2_a_4),
    .A_5(minmony2_a_5), .A_6(multiplxy_s_bit6), .D_0(binbcd2_d_0), .D_1(binbcd2_d_1), .D_2(binbcd2_d_2),
    .D_3(binbcd2_d_3), .U_0(binbcd2_u_0), .U_1(binbcd2_u_1), .U_2(binbcd2_u_2), .U_3(binbcd2_u_3));  // open: A_7, A_8, C_0, C_1, C_2
  Reset_wk_Seg2 Rst_wecker_Seg2 (
    .A_0(binbcd_d_0), .A_1(binbcd_d_1), .A_2(binbcd_d_2), .A_3(binbcd_d_3), .U_0(binbcd_u_0),
    .U_1(binbcd_u_1), .U_2(binbcd_u_2), .U_3(binbcd_u_3), .Reset_seg2(Rst_wecker_Seg2_reset_seg2));
  Reset_Wk_Seg1 rstwecker1 (
    .RsSeg1(rstwecker1_rsseg1), .A_0(binbcd_d_0), .A_3(binbcd_d_3), .A_1(binbcd_d_1), .A_2(binbcd_d_2));
  Reset_Wk_S3u4 rstwecker2 (
    .RsSeg3(rstwecker2_rsseg3), .A_0(binbcd2_d_0), .A_3(binbcd2_d_3), .A_1(binbcd2_d_1), .A_2(binbcd2_d_2));
  and and_1 (Reset_Wecker_Seg1, tstnfehler_wecker_stellen, rstwecker1_rsseg1);
  and and_2 (Reset_Wecker_Seg3_4, tstnfehler_wecker_stellen, rstwecker2_rsseg3);
  and and_3 (Reset_Wecker_Seg2, tstnfehler_wecker_stellen, Rst_wecker_Seg2_reset_seg2);
  BCD2_7Seg bcd7seg (
    .A0(binbcd_d_0), .A1(binbcd_d_1), .A2(binbcd_d_2), .A3(binbcd_d_3), .Seg_A(bcd7seg_seg_a),
    .Seg_B(bcd7seg_seg_b), .Seg_C(bcd7seg_seg_c), .Seg_D(bcd7seg_seg_d), .Seg_E(bcd7seg_seg_e),
    .Seg_F(bcd7seg_seg_f), .Seg_G(bcd7seg_seg_g));
  BCD2_7Seg bcd7seg_1 (
    .A0(binbcd_u_0), .A1(binbcd_u_1), .A2(binbcd_u_2), .A3(binbcd_u_3), .Seg_A(bcd7seg_1_seg_a),
    .Seg_B(bcd7seg_1_seg_b), .Seg_C(bcd7seg_1_seg_c), .Seg_D(bcd7seg_1_seg_d), .Seg_E(bcd7seg_1_seg_e),
    .Seg_F(bcd7seg_1_seg_f), .Seg_G(bcd7seg_1_seg_g));
  BCD2_7Seg bcd7seg2 (
    .A0(binbcd2_d_0), .A1(binbcd2_d_1), .A2(binbcd2_d_2), .A3(binbcd2_d_3), .Seg_A(bcd7seg2_seg_a),
    .Seg_B(bcd7seg2_seg_b), .Seg_C(bcd7seg2_seg_c), .Seg_D(bcd7seg2_seg_d), .Seg_E(bcd7seg2_seg_e),
    .Seg_F(bcd7seg2_seg_f), .Seg_G(bcd7seg2_seg_g));
  BCD2_7Seg bcd7seg3 (
    .A0(binbcd2_u_0), .A1(binbcd2_u_1), .A2(binbcd2_u_2), .A3(binbcd2_u_3), .Seg_A(bcd7seg3_seg_a),
    .Seg_B(bcd7seg3_seg_b), .Seg_C(bcd7seg3_seg_c), .Seg_D(bcd7seg3_seg_d), .Seg_E(bcd7seg3_seg_e),
    .Seg_F(bcd7seg3_seg_f), .Seg_G(bcd7seg3_seg_g));
  Blinken_Wecker blk (
    .Takt(Takt_Wecker_Stellen), .Wecker_Stellen(tstnfehler_wecker_stellen), .e(bcd7seg_seg_a),
    .e_1(bcd7seg_seg_b), .e_2(bcd7seg_seg_c), .e_3(bcd7seg_seg_d), .e_4(bcd7seg_seg_e), .e_5(bcd7seg_seg_f),
    .e_6(bcd7seg_seg_g), .e_7(bcd7seg_1_seg_a), .e_8(bcd7seg_1_seg_b), .e_9(bcd7seg_1_seg_c),
    .e_10(bcd7seg_1_seg_d), .e_11(bcd7seg_1_seg_e), .e_12(bcd7seg_1_seg_f), .e_13(bcd7seg_1_seg_g),
    .Seg1_A(Seg_1A), .Seg1_B(Seg_1B), .Seg1_C(Seg_1C), .Seg1_D(Seg_1D), .Seg1_E(Seg_1E), .Seg1_F(Seg_1F),
    .Seg1_G(Seg_1G), .Seg2_A(Seg_2A), .Seg2_B(Seg_2B), .Seg2_C(Seg_2C), .Seg2_D(Seg_2D), .Seg2_E(Seg_2E),
    .Seg2_F(Seg_2F), .Seg2_G(Seg_2G));
  Blinken_Wecker blk2 (
    .Takt(Takt_Wecker_Stellen), .Wecker_Stellen(tstnfehler_wecker_stellen), .e(bcd7seg2_seg_a),
    .e_1(bcd7seg2_seg_b), .e_2(bcd7seg2_seg_c), .e_3(bcd7seg2_seg_d), .e_4(bcd7seg2_seg_e),
    .e_5(bcd7seg2_seg_f), .e_6(bcd7seg2_seg_g), .e_7(bcd7seg3_seg_a), .e_8(bcd7seg3_seg_b),
    .e_9(bcd7seg3_seg_c), .e_10(bcd7seg3_seg_d), .e_11(bcd7seg3_seg_e), .e_12(bcd7seg3_seg_f),
    .e_13(bcd7seg3_seg_g), .Seg1_A(Seg_3A), .Seg1_B(Seg_3B), .Seg1_C(Seg_3C), .Seg1_D(Seg_3D),
    .Seg1_E(Seg_3E), .Seg1_F(Seg_3F), .Seg1_G(Seg_3G), .Seg2_A(Seg_4A), .Seg2_B(Seg_4B), .Seg2_C(Seg_4C),
    .Seg2_D(Seg_4D), .Seg2_E(Seg_4E), .Seg2_F(Seg_4F), .Seg2_G(Seg_4G));
endmodule

module Multiplex_Std_Tag (
  input  Eingangstaste_Min_Sek,
  input  Eingangstaste_Tag_Monat,
  input  Eingangstaste_Jahr,
  input  Wecker_Stellen,
  input  Tag_Bit0,
  input  Tag_Bit1,
  input  Tag_Bit2,
  input  Tag_Bit3,
  input  Tag_Bit4,
  input  Std_Bit0,
  input  Std_Bit1,
  input  Std_Bit2,
  input  Std_Bit3,
  input  Std_Bit4,
  input  Wecker_Std_Bit_0,
  input  Wecker_Std_Bit_1,
  input  Wecker_Std_Bit_2,
  input  Wecker_Std_Bit_3,
  input  Wecker_Std_Bit_4,
  output Bit0,
  output Bit1,
  output Bit2,
  output Bit3,
  output Bit4
);

  wire and_1_out, and_2_out, and_3_out, and_4_out, and_5_out, and_6_out, and_7_out, and_8_out, and_9_out,
       and_10_out, and_11_out, and_12_out, and_13_out, and_14_out, and_15_out;

  and and_1 (and_1_out, Tag_Bit0, ~Eingangstaste_Jahr, Eingangstaste_Tag_Monat, ~Eingangstaste_Min_Sek);  // AND_Gate
  and and_2 (and_2_out, Std_Bit0, ~Eingangstaste_Jahr, ~Eingangstaste_Tag_Monat, ~Eingangstaste_Min_Sek, ~Wecker_Stellen);  // AND_Gate
  and and_3 (and_3_out, Tag_Bit1, ~Eingangstaste_Jahr, Eingangstaste_Tag_Monat, ~Eingangstaste_Min_Sek);  // AND_Gate
  and and_4 (and_4_out, Std_Bit1, ~Eingangstaste_Jahr, ~Eingangstaste_Tag_Monat, ~Eingangstaste_Min_Sek, ~Wecker_Stellen);  // AND_Gate
  and and_5 (and_5_out, Tag_Bit2, ~Eingangstaste_Jahr, Eingangstaste_Tag_Monat, ~Eingangstaste_Min_Sek);  // AND_Gate
  and and_6 (and_6_out, Std_Bit2, ~Eingangstaste_Jahr, ~Eingangstaste_Tag_Monat, ~Eingangstaste_Min_Sek, ~Wecker_Stellen);  // AND_Gate
  and and_7 (and_7_out, Tag_Bit3, ~Eingangstaste_Jahr, Eingangstaste_Tag_Monat, ~Eingangstaste_Min_Sek);  // AND_Gate
  and and_8 (and_8_out, Std_Bit3, ~Eingangstaste_Jahr, ~Eingangstaste_Tag_Monat, ~Eingangstaste_Min_Sek, ~Wecker_Stellen);  // AND_Gate
  and and_9 (and_9_out, Tag_Bit4, ~Eingangstaste_Jahr, Eingangstaste_Tag_Monat, ~Eingangstaste_Min_Sek);  // AND_Gate
  and and_10 (and_10_out, Std_Bit4, ~Eingangstaste_Jahr, ~Eingangstaste_Tag_Monat, ~Eingangstaste_Min_Sek, ~Wecker_Stellen);  // AND_Gate
  and and_11 (and_11_out, Wecker_Stellen, Wecker_Std_Bit_0);
  and and_12 (and_12_out, Wecker_Stellen, Wecker_Std_Bit_1);
  and and_13 (and_13_out, Wecker_Stellen, Wecker_Std_Bit_2);
  and and_14 (and_14_out, Wecker_Stellen, Wecker_Std_Bit_3);
  and and_15 (and_15_out, Wecker_Stellen, Wecker_Std_Bit_4);
  or or_1 (Bit0, and_1_out, and_11_out, and_2_out);
  or or_2 (Bit1, and_3_out, and_12_out, and_4_out);
  or or_3 (Bit2, and_5_out, and_13_out, and_6_out);
  or or_4 (Bit3, and_7_out, and_14_out, and_8_out);
  or or_5 (Bit4, and_9_out, and_15_out, and_10_out);
endmodule

module Multiplex_Min_Monat (
  input  Eingangstaste_Tag_Monat,
  input  Eingangstaste_Jahr,
  input  Wecker_Stellen,
  input  Monat_Bit0,
  input  Monat_Bit1,
  input  Monat_Bit2,
  input  Monat_Bit3,
  input  Min_Bit0,
  input  Min_Bit1,
  input  Min_Bit2,
  input  Min_Bit3,
  input  Min_Bit4,
  input  Min_Bit5,
  input  Wecker_Min_Bit_0,
  input  Wecker_Min_Bit_1,
  input  Wecker_Min_Bit_2,
  input  Wecker_Min_Bit_3,
  input  Wecker_Min_Bit_4,
  input  Wecker_Min_Bit_5,
  output Bit0,
  output Bit1,
  output Bit2,
  output Bit3,
  output Bit4,
  output Bit5
);

  wire and_1_out, and_2_out, and_3_out, and_4_out, and_5_out, and_6_out, and_7_out, and_8_out, and_9_out,
       and_10_out, and_11_out, and_12_out, and_13_out, and_14_out, and_15_out, and_16_out;

  and and_1 (and_1_out, Monat_Bit0, ~Eingangstaste_Jahr, Eingangstaste_Tag_Monat);  // AND_Gate
  and and_2 (and_2_out, Min_Bit0, ~Eingangstaste_Jahr, ~Wecker_Stellen, ~Eingangstaste_Tag_Monat);  // AND_Gate
  and and_3 (and_3_out, Monat_Bit1, ~Eingangstaste_Jahr, Eingangstaste_Tag_Monat);  // AND_Gate
  and and_4 (and_4_out, Min_Bit1, ~Eingangstaste_Jahr, ~Wecker_Stellen, ~Eingangstaste_Tag_Monat);  // AND_Gate
  and and_5 (and_5_out, Monat_Bit2, ~Eingangstaste_Jahr, Eingangstaste_Tag_Monat);  // AND_Gate
  and and_6 (and_6_out, Min_Bit2, ~Eingangstaste_Jahr, ~Wecker_Stellen, ~Eingangstaste_Tag_Monat);  // AND_Gate
  and and_7 (and_7_out, Monat_Bit3, ~Eingangstaste_Jahr, Eingangstaste_Tag_Monat);  // AND_Gate
  and and_8 (and_8_out, Min_Bit3, ~Eingangstaste_Jahr, ~Wecker_Stellen, ~Eingangstaste_Tag_Monat);  // AND_Gate
  and and_9 (and_9_out, Min_Bit4, ~Eingangstaste_Jahr, ~Wecker_Stellen, ~Eingangstaste_Tag_Monat);  // AND_Gate
  and and_10 (and_10_out, Min_Bit5, ~Eingangstaste_Jahr, ~Wecker_Stellen, ~Eingangstaste_Tag_Monat);  // AND_Gate
  and and_11 (and_11_out, Wecker_Stellen, Wecker_Min_Bit_0);
  and and_12 (and_12_out, Wecker_Stellen, Wecker_Min_Bit_1);
  and and_13 (and_13_out, Wecker_Stellen, Wecker_Min_Bit_2);
  and and_14 (and_14_out, Wecker_Stellen, Wecker_Min_Bit_3);
  and and_15 (and_15_out, Wecker_Stellen, Wecker_Min_Bit_4);
  and and_16 (and_16_out, Wecker_Stellen, Wecker_Min_Bit_5);
  or or_1 (Bit0, and_1_out, and_11_out, and_2_out);
  or or_2 (Bit1, and_3_out, and_12_out, and_4_out);
  or or_3 (Bit2, and_5_out, and_13_out, and_6_out);
  or or_4 (Bit3, and_7_out, and_14_out, and_8_out);
  or or_5 (Bit4, and_9_out, and_15_out);
  or or_6 (Bit5, and_10_out, and_16_out);
endmodule

module Multiplex_Jahr_Sekunden (
  input  Eingangstaste_Jahr,
  input  Eingangstaste_Min_Sek,
  input  Jahr_Bit0,
  input  Jahr_Bit1,
  input  Jahr_Bit2,
  input  Jahr_Bit3,
  input  Jahr_Bit4,
  input  Jahr_Bit5,
  input  Jahr_Bit6,
  input  Sekunden_Bit_0,
  input  Sekunden_Bit_1,
  input  Sekunden_Bit_2,
  input  Sekunden_Bit_3,
  input  Sekunden_Bit_4,
  input  Sekunden_Bit_5,
  output Bit0,
  output Bit1,
  output Bit2,
  output Bit3,
  output Bit4,
  output Bit5,
  output Bit6
);

  wire and_1_out, and_2_out, and_3_out, and_4_out, and_5_out, and_6_out, mltplxs_bit_0, mltplxs_bit_1,
       mltplxs_bit_2, mltplxs_bit_3, mltplxs_bit_4, mltplxs_bit_5;

  and and_1 (and_1_out, Jahr_Bit0, Eingangstaste_Jahr);
  and and_2 (and_2_out, Jahr_Bit1, Eingangstaste_Jahr);
  and and_3 (and_3_out, Jahr_Bit2, Eingangstaste_Jahr);
  and and_4 (and_4_out, Jahr_Bit3, Eingangstaste_Jahr);
  and and_5 (and_5_out, Jahr_Bit4, Eingangstaste_Jahr);
  and and_6 (and_6_out, Jahr_Bit5, Eingangstaste_Jahr);
  and and_7 (Bit6, Jahr_Bit6, Eingangstaste_Jahr);
  Multiplex_Sekunden mltplxs (
    .Taste_Min_Sek(Eingangstaste_Min_Sek), .Sek_Bit_0(Sekunden_Bit_0), .Sek_Bit_1(Sekunden_Bit_1),
    .Sek_Bit_2(Sekunden_Bit_2), .Sek_Bit_3(Sekunden_Bit_3), .Sek_Bit_4(Sekunden_Bit_4),
    .Sek_Bit_5(Sekunden_Bit_5), .Bit_0(mltplxs_bit_0), .Bit_1(mltplxs_bit_1), .Bit_2(mltplxs_bit_2),
    .Bit_3(mltplxs_bit_3), .Bit_4(mltplxs_bit_4), .Bit_5(mltplxs_bit_5));
  or or_1 (Bit0, and_1_out, mltplxs_bit_0);
  or or_2 (Bit1, and_2_out, mltplxs_bit_1);
  or or_3 (Bit2, and_3_out, mltplxs_bit_2);
  or or_4 (Bit3, and_4_out, mltplxs_bit_3);
  or or_5 (Bit4, and_5_out, mltplxs_bit_4);
  or or_6 (Bit5, and_6_out, mltplxs_bit_5);
endmodule

module Verknuepfung_min_mon_jahr (
  input  e,
  input  e_1,
  input  e_2,
  input  e_3,
  input  e_4,
  input  e_5,
  input  e_6,
  input  e_7,
  input  e_8,
  input  e_9,
  input  e_10,
  input  e_11,
  output a,
  output a_1,
  output a_2,
  output a_3,
  output a_4,
  output a_5
);

  or or_1 (a, e, e_1);
  or or_2 (a_1, e_2, e_3);
  or or_3 (a_2, e_4, e_5);
  or or_4 (a_3, e_6, e_7);
  or or_5 (a_4, e_8, e_9);
  or or_6 (a_5, e_10, e_11);
endmodule

module Testing7Seg (
  input  Eingang,
  input  Eingang_1,
  input  Eingang_2,
  input  Eingang_3,
  input  Eingang_4,
  input  Eingang_5,
  input  [4:0] Eingang_6,
  input  [4:0] Eingang_7,
  input  [5:0] Eingang_8,
  input  [5:0] Eingang_9,
  input  [5:0] Eingang_10,
  input  [4:0] Eingang_11,
  input  [3:0] Eingang_12,
  input  [6:0] Eingang_13
);

  wire hauptschaltung_7seg_anzeige_1_seg_1a, hauptschaltung_7seg_anzeige_1_seg_1b,
       hauptschaltung_7seg_anzeige_1_seg_1c, hauptschaltung_7seg_anzeige_1_seg_1d,
       hauptschaltung_7seg_anzeige_1_seg_1e, hauptschaltung_7seg_anzeige_1_seg_1f,
       hauptschaltung_7seg_anzeige_1_seg_1g, hauptschaltung_7seg_anzeige_1_seg_2a,
       hauptschaltung_7seg_anzeige_1_seg_2b, hauptschaltung_7seg_anzeige_1_seg_2c,
       hauptschaltung_7seg_anzeige_1_seg_2d, hauptschaltung_7seg_anzeige_1_seg_2e,
       hauptschaltung_7seg_anzeige_1_seg_2f, hauptschaltung_7seg_anzeige_1_seg_2g,
       hauptschaltung_7seg_anzeige_1_seg_3a, hauptschaltung_7seg_anzeige_1_seg_3b,
       hauptschaltung_7seg_anzeige_1_seg_3c, hauptschaltung_7seg_anzeige_1_seg_3d,
       hauptschaltung_7seg_anzeige_1_seg_3e, hauptschaltung_7seg_anzeige_1_seg_3f,
       hauptschaltung_7seg_anzeige_1_seg_3g, hauptschaltung_7seg_anzeige_1_seg_4a,
       hauptschaltung_7seg_anzeige_1_seg_4b, hauptschaltung_7seg_anzeige_1_seg_4c,
       hauptschaltung_7seg_anzeige_1_seg_4d, hauptschaltung_7seg_anzeige_1_seg_4e,
       hauptschaltung_7seg_anzeige_1_seg_4f, hauptschaltung_7seg_anzeige_1_seg_4g;

  _7_Segment_Display u_7_segment_display_1 (
    .g(hauptschaltung_7seg_anzeige_1_seg_1g), .f(hauptschaltung_7seg_anzeige_1_seg_1f),
    .a(hauptschaltung_7seg_anzeige_1_seg_1a), .b(hauptschaltung_7seg_anzeige_1_seg_1b),
    .e(hauptschaltung_7seg_anzeige_1_seg_1e), .d(hauptschaltung_7seg_anzeige_1_seg_1d),
    .c(hauptschaltung_7seg_anzeige_1_seg_1c));  // open: dp
  _7_Segment_Display u_7_segment_display_2 (
    .g(hauptschaltung_7seg_anzeige_1_seg_2g), .f(hauptschaltung_7seg_anzeige_1_seg_2f),
    .a(hauptschaltung_7seg_anzeige_1_seg_2a), .b(hauptschaltung_7seg_anzeige_1_seg_2b),
    .e(hauptschaltung_7seg_anzeige_1_seg_2e), .d(hauptschaltung_7seg_anzeige_1_seg_2d),
    .c(hauptschaltung_7seg_anzeige_1_seg_2c));  // open: dp
  _7_Segment_Display u_7_segment_display_3 (
    .g(hauptschaltung_7seg_anzeige_1_seg_3g), .f(hauptschaltung_7seg_anzeige_1_seg_3f),
    .a(hauptschaltung_7seg_anzeige_1_seg_3a), .b(hauptschaltung_7seg_anzeige_1_seg_3b),
    .e(hauptschaltung_7seg_anzeige_1_seg_3e), .d(hauptschaltung_7seg_anzeige_1_seg_3d),
    .c(hauptschaltung_7seg_anzeige_1_seg_3c));  // open: dp
  _7_Segment_Display u_7_segment_display_4 (
    .g(hauptschaltung_7seg_anzeige_1_seg_4g), .f(hauptschaltung_7seg_anzeige_1_seg_4f),
    .a(hauptschaltung_7seg_anzeige_1_seg_4a), .b(hauptschaltung_7seg_anzeige_1_seg_4b),
    .e(hauptschaltung_7seg_anzeige_1_seg_4e), .d(hauptschaltung_7seg_anzeige_1_seg_4d),
    .c(hauptschaltung_7seg_anzeige_1_seg_4c));  // open: dp
  Hauptschaltung_7Seg_Anzeige hauptschaltung_7seg_anzeige_1 (
    .Seg_1C(hauptschaltung_7seg_anzeige_1_seg_1c), .Seg_2E(hauptschaltung_7seg_anzeige_1_seg_2e),
    .Schalter_Gecko_Wecker_Stellem(Eingang_4), .Seg_1B(hauptschaltung_7seg_anzeige_1_seg_1b),
    .Seg_1A(hauptschaltung_7seg_anzeige_1_seg_1a), .Seg_2B(hauptschaltung_7seg_anzeige_1_seg_2b),
    .Takt_Wecker_Stellen(Eingang), .Seg_2A(hauptschaltung_7seg_anzeige_1_seg_2a),
    .Seg_1G(hauptschaltung_7seg_anzeige_1_seg_1g), .Seg_2G(hauptschaltung_7seg_anzeige_1_seg_2g),
    .Taste_Gecko_Jahr(Eingang_3), .Seg_1E(hauptschaltung_7seg_anzeige_1_seg_1e),
    .Taste_Gecko_Min_Sek(Eingang_1), .Seg_2F(hauptschaltung_7seg_anzeige_1_seg_2f),
    .Taste_Gecko_Tag_Mon(Eingang_2), .Seg_1D(hauptschaltung_7seg_anzeige_1_seg_1d),
    .Seg_2C(hauptschaltung_7seg_anzeige_1_seg_2c), .Schalter_Gecko_Wecker_Ein_Aus(Eingang_5),
    .Seg_2D(hauptschaltung_7seg_anzeige_1_seg_2d), .Seg_1F(hauptschaltung_7seg_anzeige_1_seg_1f),
    .Seg_3A(hauptschaltung_7seg_anzeige_1_seg_3a), .Seg_3B(hauptschaltung_7seg_anzeige_1_seg_3b),
    .Seg_3C(hauptschaltung_7seg_anzeige_1_seg_3c), .Seg_3D(hauptschaltung_7seg_anzeige_1_seg_3d),
    .Seg_3E(hauptschaltung_7seg_anzeige_1_seg_3e), .Seg_3F(hauptschaltung_7seg_anzeige_1_seg_3f),
    .Seg_3G(hauptschaltung_7seg_anzeige_1_seg_3g), .Seg_4A(hauptschaltung_7seg_anzeige_1_seg_4a),
    .Seg_4B(hauptschaltung_7seg_anzeige_1_seg_4b), .Seg_4C(hauptschaltung_7seg_anzeige_1_seg_4c),
    .Seg_4D(hauptschaltung_7seg_anzeige_1_seg_4d), .Seg_4E(hauptschaltung_7seg_anzeige_1_seg_4e),
    .Seg_4F(hauptschaltung_7seg_anzeige_1_seg_4f), .Seg_4G(hauptschaltung_7seg_anzeige_1_seg_4g),
    .Stundenbits(Eingang_6), .Wecker_Stundenbits(Eingang_7), .Minutenbits(Eingang_8),
    .Wecker_Minutenbits(Eingang_9), .Sekundenbits(Eingang_10), .Jahrbits(Eingang_13), .Tagbits(Eingang_11),
    .Monatbits(Eingang_12));  // open: Weckerfunktion_zu_LED, Min_sek_zu_LED, Tag_Mon_zu_LED, Jahr_zu_LED, Reset_Wecker_Seg1, Reset_Wecker_Seg3_4, Reset_Wecker_Seg2
endmodule

module BCD2_7Seg (
  input  A0,
  input  A1,
  input  A2,
  input  A3,
  output Seg_A,
  output Seg_B,
  output Seg_C,
  output Seg_D,
  output Seg_E,
  output Seg_F,
  output Seg_G
);

  wire nand_1_out, nand_2_out, nand_3_out, nand_4_out, nor_1_out, nor_2_out, nor_3_out, nor_4_out, nor_5_out,
       nor_6_out, nor_7_out, nor_8_out, nor_9_out, nor_10_out, nor_11_out, nor_12_out, nor_13_out,
       nor_14_out, nor_15_out, nor_16_out, nor_17_out, nor_18_out, nor_19_out, nor_20_out, nor_21_out,
       nor_22_out, nor_23_out, nor_24_out, nor_25_out, nor_26_out, nor_27_out, nor_28_out, nor_29_out,
       nor_33_out;

  nor nor_1 (nor_1_out, A0, A0);
  nor nor_2 (nor_2_out, A2, A2);
  nor nor_3 (nor_3_out, A0, A0);
  nor nor_4 (nor_4_out, A2, A2);
  nor nor_5 (nor_5_out, A1, A1);
  nor nor_6 (nor_6_out, A2, A2);
  nor nor_7 (nor_7_out, A1, A1);
  nor nor_8 (nor_8_out, A0, A0);
  nor nor_9 (nor_9_out, A2, A2);
  nor nor_10 (nor_10_out, A0, A0);
  nor nor_11 (nor_11_out, A1, A1);
  nor nor_12 (nor_12_out, A2, A2);
  nand nand_1 (nand_1_out, A0, A0);
  nand nand_2 (nand_2_out, A2, A2);
  nor nor_13 (nor_13_out, A1, A1);
  nor nor_14 (nor_14_out, A0, A0);
  nor nor_15 (nor_15_out, A1, A2, A3);
  nor nor_16 (nor_16_out, A0, A0);
  nor nor_17 (nor_17_out, A1, A1);
  nor nor_18 (nor_18_out, A2, A2);
  nor nor_19 (nor_19_out, nor_1_out, A1, A2, A3);
  nor nor_20 (nor_20_out, A3, A0, A1, nor_2_out);
  nor nor_21 (nor_21_out, nor_3_out, A1, A3, nor_4_out);
  nor nor_22 (nor_22_out, nor_5_out, nor_6_out, A0, A3);
  nor nor_23 (nor_23_out, nor_7_out, A0, A2, A3);
  nor nor_24 (nor_24_out, nor_8_out, A1, A2, A3);
  nor nor_25 (nor_25_out, nor_9_out, A0, A1, A3);
  nand nand_3 (nand_3_out, A1, nand_1_out);
  nand nand_4 (nand_4_out, nand_1_out, nand_2_out);
  nor nor_26 (nor_26_out, A2, nor_13_out);
  nor nor_27 (nor_27_out, nor_13_out, nor_14_out);
  nor nor_28 (nor_28_out, nor_14_out, A2, A3);
  nor nor_29 (nor_29_out, nor_16_out, nor_17_out, nor_18_out);
  nor nor_30 (Seg_A, nor_19_out, nor_20_out);
  nor nor_31 (Seg_B, nor_21_out, nor_22_out);
  nor nor_32 (Seg_C, nor_23_out, nor_23_out);
  nor nor_33 (nor_33_out, nor_10_out, nor_11_out, nor_12_out, A3);
  nand nand_5 (Seg_E, nand_3_out, nand_4_out);
  nor nor_34 (Seg_F, nor_26_out, nor_27_out, nor_28_out);
  nor nor_35 (Seg_G, nor_15_out, nor_29_out);
  nor nor_36 (Seg_D, nor_24_out, nor_25_out, nor_33_out);
endmodule

module Bin2_BCD (
  input  A_0,
  input  A_1,
  input  A_2,
  input  A_3,
  input  A_4,
  input  A_5,
  input  A_6,
  input  A_7,
  input  A_8,
  output C_0,
  output C_1,
  output C_2,
  output D_0,
  output D_1,
  output D_2,
  output D_3,
  output U_0,
  output U_1,
  output U_2,
  output U_3
);

  wire teil_1_s_0, teil_1_s_1, teil_1_s_2, teil_1_s_3, teil_2_s_0, teil_2_s_1, teil_2_s_2, teil_2_s_3,
       teil_3_s_0, teil_3_s_1, teil_3_s_2, teil_3_s_3, teil_4_s_0, teil_4_s_1, teil_4_s_2, teil_4_s_3,
       teil_5_s_0, teil_5_s_1, teil_5_s_2, teil_6_s_0, teil_6_s_1, teil_6_s_2, teil_6_s_3, teil_7_s_0,
       teil_7_s_1, teil_7_s_2, teil_7_s_3, teil_s_0, teil_s_1, teil_s_2, teil_s_3;

  BCD_Teil teil_5 (.A_0(teil_3_s_3), .S_0(teil_5_s_0), .S_1(teil_5_s_1), .S_2(teil_5_s_2));  // open: A_1, A_2, A_3, S_3
  BCD_Teil teil_8 (
    .A_0(teil_6_s_3), .A_1(teil_5_s_0), .A_2(teil_5_s_1), .A_3(teil_5_s_2), .S_0(C_1), .S_1(C_2));  // open: S_2, S_3
  BCD_Teil teil (
    .A_0(A_6), .A_1(A_7), .A_2(A_8), .S_0(teil_s_0), .S_1(teil_s_1), .S_2(teil_s_2), .S_3(teil_s_3));  // open: A_3
  BCD_Teil teil_1 (
    .A_0(A_5), .A_1(teil_s_0), .A_2(teil_s_1), .A_3(teil_s_2), .S_0(teil_1_s_0), .S_1(teil_1_s_1),
    .S_2(teil_1_s_2), .S_3(teil_1_s_3));
  BCD_Teil teil_2 (
    .A_0(A_4), .A_1(teil_1_s_0), .A_2(teil_1_s_1), .A_3(teil_1_s_2), .S_0(teil_2_s_0), .S_1(teil_2_s_1),
    .S_2(teil_2_s_2), .S_3(teil_2_s_3));
  BCD_Teil teil_3 (
    .A_0(teil_2_s_3), .A_1(teil_1_s_3), .A_2(teil_s_3), .S_0(teil_3_s_0), .S_1(teil_3_s_1), .S_2(teil_3_s_2),
    .S_3(teil_3_s_3));  // open: A_3
  BCD_Teil teil_6 (
    .A_0(teil_4_s_3), .A_1(teil_3_s_0), .A_2(teil_3_s_1), .A_3(teil_3_s_2), .S_0(teil_6_s_0),
    .S_1(teil_6_s_1), .S_2(teil_6_s_2), .S_3(teil_6_s_3));
  BCD_Teil teil_9 (
    .A_0(teil_7_s_3), .A_1(teil_6_s_0), .A_2(teil_6_s_1), .A_3(teil_6_s_2), .S_0(D_1), .S_1(D_2), .S_2(D_3),
    .S_3(C_0));
  BCD_Teil teil_4 (
    .A_0(A_3), .A_1(teil_2_s_0), .A_2(teil_2_s_1), .A_3(teil_2_s_2), .S_0(teil_4_s_0), .S_1(teil_4_s_1),
    .S_2(teil_4_s_2), .S_3(teil_4_s_3));
  BCD_Teil teil_7 (
    .A_0(A_2), .A_1(teil_4_s_0), .A_2(teil_4_s_1), .A_3(teil_4_s_2), .S_0(teil_7_s_0), .S_1(teil_7_s_1),
    .S_2(teil_7_s_2), .S_3(teil_7_s_3));
  BCD_Teil teil_10 (
    .A_0(A_1), .A_1(teil_7_s_0), .A_2(teil_7_s_1), .A_3(teil_7_s_2), .S_0(U_1), .S_1(U_2), .S_2(U_3),
    .S_3(D_0));

  assign U_0 = A_0;
endmodule

module BCD_Teil (
  input  A_0,
  input  A_1,
  input  A_2,
  input  A_3,
  output S_0,
  output S_1,
  output S_2,
  output S_3
);

  wire and_1_out, and_2_out, and_3_out, and_4_out, and_5_out, and_6_out, and_7_out, not_1_out, not_2_out,
       not_3_out, not_4_out, or_1_out, or_2_out, or_3_out;

  not not_1 (not_1_out, A_0);
  not not_2 (not_2_out, A_1);
  not not_3 (not_3_out, A_2);
  not not_4 (not_4_out, A_3);
  and and_1 (and_1_out, A_0, not_3_out, not_4_out);
  and and_2 (and_2_out, not_1_out, A_3);
  and and_3 (and_3_out, not_1_out, A_1, A_2);
  or or_1 (or_1_out, A_1, A_3);
  or or_2 (or_2_out, A_0, not_3_out);
  or or_3 (or_3_out, not_1_out, not_4_out);
  and and_4 (and_4_out, not_1_out, not_2_out, A_2);
  and and_5 (and_5_out, A_0, A_3);
  and and_6 (and_6_out, A_0, A_2);
  and and_7 (and_7_out, A_1, A_2);
  or or_4 (S_0, and_1_out, and_2_out, and_3_out);
  and and_8 (S_1, or_1_out, or_2_out, or_3_out);
  or or_5 (S_2, and_4_out, and_5_out);
  or or_6 (S_3, and_6_out, and_7_out, A_3);
endmodule

module Umschaltung_Min (
  input  Taste_Min_Sek,
  input  Bit_0,
  input  Bit_1,
  input  Bit_2,
  input  Bit_3,
  input  Bit_4,
  input  Bit_5,
  output Seg1_Bit_0,
  output Seg1_Bit_1,
  output Seg1_Bit_2,
  output Seg1_Bit_3,
  output Seg1_Bit_4,
  output Seg1_Bit_5,
  output Seg2_Bit_0,
  output Seg2_Bit_1,
  output Seg2_Bit_2,
  output Seg2_Bit_3,
  output Seg2_Bit_4,
  output Seg2_Bit_5
);

  and and_1 (Seg1_Bit_0, Taste_Min_Sek, Bit_0);
  and and_2 (Seg2_Bit_0, ~Taste_Min_Sek, Bit_0);  // AND_Gate
  and and_3 (Seg1_Bit_1, Taste_Min_Sek, Bit_1);
  and and_4 (Seg2_Bit_1, ~Taste_Min_Sek, Bit_1);  // AND_Gate
  and and_5 (Seg1_Bit_2, Taste_Min_Sek, Bit_2);
  and and_6 (Seg2_Bit_2, ~Taste_Min_Sek, Bit_2);  // AND_Gate
  and and_7 (Seg1_Bit_3, Taste_Min_Sek, Bit_3);
  and and_8 (Seg2_Bit_3, ~Taste_Min_Sek, Bit_3);  // AND_Gate
  and and_9 (Seg1_Bit_4, Taste_Min_Sek, Bit_4);
  and and_10 (Seg2_Bit_4, ~Taste_Min_Sek, Bit_4);  // AND_Gate
  and and_11 (Seg1_Bit_5, Taste_Min_Sek, Bit_5);
  and and_12 (Seg2_Bit_5, ~Taste_Min_Sek, Bit_5);  // AND_Gate
endmodule

module Multiplex_Sekunden (
  input  Taste_Min_Sek,
  input  Sek_Bit_0,
  input  Sek_Bit_1,
  input  Sek_Bit_2,
  input  Sek_Bit_3,
  input  Sek_Bit_4,
  input  Sek_Bit_5,
  output Bit_0,
  output Bit_1,
  output Bit_2,
  output Bit_3,
  output Bit_4,
  output Bit_5
);

  and and_1 (Bit_0, Sek_Bit_0, Taste_Min_Sek);
  and and_2 (Bit_1, Sek_Bit_1, Taste_Min_Sek);
  and and_3 (Bit_2, Sek_Bit_2, Taste_Min_Sek);
  and and_4 (Bit_3, Sek_Bit_3, Taste_Min_Sek);
  and and_5 (Bit_4, Sek_Bit_4, Taste_Min_Sek);
  and and_6 (Bit_5, Sek_Bit_5, Taste_Min_Sek);
endmodule

module Tastenfehler (
  input  Taste_Gecko_Min_Sek,
  input  Taste_Gecko_Tag_Mon,
  input  Taste_Gecko_Jahr,
  input  Schalter_Gecko_Wecker_Stellen,
  output Taste_Min_Sek,
  output Taste_Tag_Mon,
  output Taste_Jahr,
  output Wecker_Stellen
);

  and and_1 (Taste_Min_Sek, Taste_Gecko_Min_Sek, ~Taste_Gecko_Tag_Mon, ~Taste_Gecko_Jahr, ~Schalter_Gecko_Wecker_Stellen);  // AND_Gate
  and and_2 (Taste_Tag_Mon, ~Taste_Gecko_Min_Sek, Taste_Gecko_Tag_Mon, ~Taste_Gecko_Jahr, ~Schalter_Gecko_Wecker_Stellen);  // AND_Gate
  and and_3 (Taste_Jahr, ~Taste_Gecko_Min_Sek, ~Taste_Gecko_Tag_Mon, Taste_Gecko_Jahr, ~Schalter_Gecko_Wecker_Stellen);  // AND_Gate

  assign Wecker_Stellen = Schalter_Gecko_Wecker_Stellen;
endmodule

module Weckfunktion_Zeitvergleich (
  input  Wecker_Ein_Aus,
  input  Stunde_Aktuell_0,
  input  Stunde_Aktuell_1,
  input  Stunde_Aktuell_2,
  input  Stunde_Aktuell_3,
  input  Stunde_Aktuell_4,
  input  Stunde_Wecker_0,
  input  Stunde_Wecker_1,
  input  Stunde_Wecker_2,
  input  Stunde_Wecker_3,
  input  Stunde_Wecker_4,
  input  MInute_Aktuell_0,
  input  MInute_Aktuell_1,
  input  MInute_Aktuell_2,
  input  MInute_Aktuell_3,
  input  MInute_Aktuell_4,
  input  MInute_Aktuell_5,
  input  MInute_Wecker_0,
  input  MInute_Wecker_1,
  input  MInute_Wecker_2,
  input  MInute_Wecker_3,
  input  MInute_Wecker_4,
  input  MInute_Wecker_5,
  output Nach_LED_Anzeige_Weckfunktion
);

  wire and_1_out, and_3_out, xnor_1_out, xnor_2_out, xnor_3_out, xnor_4_out, xnor_5_out, xnor_6_out,
       xnor_7_out, xnor_8_out, xnor_9_out, xnor_10_out, xnor_11_out;

  xnor xnor_1 (xnor_1_out, Stunde_Aktuell_0, Stunde_Wecker_0);
  xnor xnor_2 (xnor_2_out, Stunde_Aktuell_1, Stunde_Wecker_1);
  xnor xnor_3 (xnor_3_out, Stunde_Aktuell_2, Stunde_Wecker_2);
  xnor xnor_4 (xnor_4_out, Stunde_Aktuell_3, Stunde_Wecker_3);
  xnor xnor_5 (xnor_5_out, Stunde_Aktuell_4, Stunde_Wecker_4);
  xnor xnor_6 (xnor_6_out, MInute_Aktuell_0, MInute_Wecker_0);
  xnor xnor_7 (xnor_7_out, MInute_Aktuell_1, MInute_Wecker_1);
  xnor xnor_8 (xnor_8_out, MInute_Aktuell_2, MInute_Wecker_2);
  xnor xnor_9 (xnor_9_out, MInute_Aktuell_3, MInute_Wecker_3);
  xnor xnor_10 (xnor_10_out, MInute_Aktuell_4, MInute_Wecker_4);
  xnor xnor_11 (xnor_11_out, MInute_Aktuell_5, MInute_Wecker_5);
  and and_1 (and_1_out, Wecker_Ein_Aus, xnor_1_out, xnor_2_out, xnor_3_out, xnor_4_out, xnor_5_out);
  and and_2 (Nach_LED_Anzeige_Weckfunktion, and_1_out, and_3_out);
  and and_3 (and_3_out, xnor_6_out, xnor_7_out, xnor_8_out, xnor_9_out, xnor_10_out, xnor_11_out);
endmodule

module Blinken_Wecker (
  input  Takt,
  input  Wecker_Stellen,
  input  e,
  input  e_1,
  input  e_2,
  input  e_3,
  input  e_4,
  input  e_5,
  input  e_6,
  input  e_7,
  input  e_8,
  input  e_9,
  input  e_10,
  input  e_11,
  input  e_12,
  input  e_13,
  output Seg1_A,
  output Seg1_B,
  output Seg1_C,
  output Seg1_D,
  output Seg1_E,
  output Seg1_F,
  output Seg1_G,
  output Seg2_A,
  output Seg2_B,
  output Seg2_C,
  output Seg2_D,
  output Seg2_E,
  output Seg2_F,
  output Seg2_G
);

  wire and_1_out, and_2_out, and_3_out, and_4_out, and_5_out, and_6_out, and_7_out, and_8_out, and_9_out,
       and_10_out, and_11_out, and_12_out, and_13_out, and_14_out, and_15_out, and_16_out, and_17_out,
       and_18_out, and_19_out, and_20_out, and_21_out, and_22_out, and_23_out, and_24_out, and_25_out,
       and_26_out, and_27_out, and_28_out;

  and and_1 (and_1_out, ~Wecker_Stellen, e);  // AND_Gate
  and and_2 (and_2_out, ~Wecker_Stellen, e_1);  // AND_Gate
  and and_3 (and_3_out, ~Wecker_Stellen, e_2);  // AND_Gate
  and and_4 (and_4_out, ~Wecker_Stellen, e_3);  // AND_Gate
  and and_5 (and_5_out, ~Wecker_Stellen, e_4);  // AND_Gate
  and and_6 (and_6_out, ~Wecker_Stellen, e_5);  // AND_Gate
  and and_7 (and_7_out, ~Wecker_Stellen, e_6);  // AND_Gate
  and and_8 (and_8_out, ~Wecker_Stellen, e_7);  // AND_Gate
  and and_9 (and_9_out, ~Wecker_Stellen, e_8);  // AND_Gate
  and and_10 (and_10_out, ~Wecker_Stellen, e_9);  // AND_Gate
  and and_11 (and_11_out, ~Wecker_Stellen, e_10);  // AND_Gate
  and and_12 (and_12_out, ~Wecker_Stellen, e_11);  // AND_Gate
  and and_13 (and_13_out, ~Wecker_Stellen, e_12);  // AND_Gate
  and and_14 (and_14_out, ~Wecker_Stellen, e_13);  // AND_Gate
  and and_15 (and_15_out, Wecker_Stellen, Takt, e);
  and and_16 (and_16_out, Wecker_Stellen, Takt, e_1);
  and and_17 (and_17_out, Wecker_Stellen, Takt, e_2);
  and and_18 (and_18_out, Wecker_Stellen, Takt, e_3);
  and and_19 (and_19_out, Wecker_Stellen, Takt, e_4);
  and and_20 (and_20_out, Wecker_Stellen, Takt, e_5);
  and and_21 (and_21_out, Wecker_Stellen, Takt, e_6);
  and and_22 (and_22_out, Wecker_Stellen, Takt, e_7);
  and and_23 (and_23_out, Wecker_Stellen, Takt, e_8);
  and and_24 (and_24_out, Wecker_Stellen, Takt, e_9);
  and and_25 (and_25_out, Wecker_Stellen, Takt, e_10);
  and and_26 (and_26_out, Wecker_Stellen, Takt, e_11);
  and and_27 (and_27_out, Wecker_Stellen, Takt, e_12);
  and and_28 (and_28_out, Wecker_Stellen, Takt, e_13);
  or or_1 (Seg1_A, and_1_out, and_15_out);
  or or_2 (Seg1_B, and_2_out, and_16_out);
  or or_3 (Seg1_C, and_3_out, and_17_out);
  or or_4 (Seg1_D, and_4_out, and_18_out);
  or or_5 (Seg1_E, and_5_out, and_19_out);
  or or_6 (Seg1_F, and_6_out, and_20_out);
  or or_7 (Seg1_G, and_7_out, and_21_out);
  or or_8 (Seg2_A, and_8_out, and_22_out);
  or or_9 (Seg2_B, and_9_out, and_23_out);
  or or_10 (Seg2_C, and_10_out, and_24_out);
  or or_11 (Seg2_D, and_11_out, and_25_out);
  or or_12 (Seg2_E, and_12_out, and_26_out);
  or or_13 (Seg2_F, and_13_out, and_27_out);
  or or_14 (Seg2_G, and_14_out, and_28_out);
endmodule

module Reset_Wk_Seg1 (
  input  A_0,
  input  A_1,
  input  A_2,
  input  A_3,
  output RsSeg1
);

  wire and_1_out, and_2_out, and_3_out, or_1_out;

  and and_1 (and_1_out, ~A_0, ~A_1, ~A_2, ~A_3);  // AND_Gate
  or or_1 (or_1_out, and_1_out, and_2_out, and_3_out);
  and and_2 (and_2_out, A_0, ~A_1, ~A_2, ~A_3);  // AND_Gate
  and and_3 (and_3_out, ~A_0, A_1, ~A_2, ~A_3);  // AND_Gate
  not not_1 (RsSeg1, or_1_out);
endmodule

module Reset_Wk_S3u4 (
  input  A_0,
  input  A_1,
  input  A_2,
  input  A_3,
  output RsSeg3
);

  wire and_1_out, and_2_out, and_3_out, and_4_out, and_5_out, and_6_out, or_1_out;

  and and_1 (and_1_out, ~A_0, ~A_1, ~A_2, ~A_3);  // AND_Gate
  and and_2 (and_2_out, A_0, ~A_1, ~A_2, ~A_3);  // AND_Gate
  and and_3 (and_3_out, ~A_0, A_1, ~A_2, ~A_3);  // AND_Gate
  and and_4 (and_4_out, A_0, A_1, ~A_2, ~A_3);  // AND_Gate
  and and_5 (and_5_out, ~A_0, ~A_1, A_2, ~A_3);  // AND_Gate
  and and_6 (and_6_out, A_0, ~A_1, A_2, ~A_3);  // AND_Gate
  not not_1 (RsSeg3, or_1_out);
  or or_1 (or_1_out, and_1_out, and_2_out, and_3_out, and_4_out, and_5_out, and_6_out);
endmodule

module Reset_wk_Seg2 (
  input  A_0,
  input  A_1,
  input  A_2,
  input  A_3,
  input  U_0,
  input  U_1,
  input  U_2,
  input  U_3,
  output Reset_seg2
);

  wire and_1_out, and_2_out, and_3_out, and_4_out, and_5_out, not_1_out, or_1_out;

  and and_1 (and_1_out, ~A_0, A_1, ~A_2, ~A_3);  // AND_Gate
  and and_2 (and_2_out, ~U_0, ~U_1, ~U_2, ~U_3);  // AND_Gate
  and and_3 (and_3_out, U_0, ~U_1, ~U_2, ~U_3);  // AND_Gate
  and and_4 (and_4_out, ~U_0, U_1, ~U_2, ~U_3);  // AND_Gate
  and and_5 (and_5_out, U_0, U_1, ~U_2, ~U_3);  // AND_Gate
  or or_1 (or_1_out, and_2_out, and_3_out, and_4_out, and_5_out);
  not not_1 (not_1_out, or_1_out);
  and and_6 (Reset_seg2, and_1_out, not_1_out);
endmodule
