// Logisim project LED_Anzeige.circ as structural Verilog: 6 circuits, main circuit Part_LED_7Seg_Buntr1
module Hauptschaltung_LED_Anzeige (
  input  Takt_blinken,
  input  Weckfunktion_Ein,
  input  Eingangstaste_Min_Sek,
  input  Eingangstaste_Tag_Monat,
  input  Eingangstaste_Jahr,
  output LED_Rahmen_Rest_Wecker,
  output LED_3_2,
  output LED_3_3,
  output LED_3_7,
  output LED_3_11,
  output LED_4_2,
  output LED_4_4,
  output LED_4_7,
  output LED_4_8,
  output LED_4_9,
  output LED_4_10,
  output LED_4_11,
  output LED_5_2,
  output LED_5_3,
  output LED_5_4,
  output LED_5_5,
  output LED_5_6,
  output LED_5_7,
  output LED_5_8,
  output LED_5_9,
  output LED_5_10,
  output LED_5_11,
  output LED_6_2,
  output LED_6_3,
  output LED_6_4,
  output LED_6_5,
  output LED_6_6,
  output LED_6_7,
  output LED_6_8,
  output LED_6_9,
  output LED_6_10,
  output LED_6_11,
  output LED_7_2,
  output LED_7_4,
  output LED_7_5,
  output LED_7_6,
  output LED_7_7,
  output LED_7_9,
  output LED_7_10,
  output LED_7_11,
  output LED_8_2,
  output LED_8_3,
  output LED_8_5,
  output LED_8_6,
  output LED_8_7,
  output LED_8_8,
  output LED_8_9,
  output LED_8_10,
  output LED_8_11
);

  wire D_und_M_1_led_3_2, D_und_M_1_led_3_3, D_und_M_1_led_3_7, D_und_M_1_led_3_11, D_und_M_1_led_4_2,
       D_und_M_1_led_4_4, D_und_M_1_led_4_7, D_und_M_1_led_4_8, D_und_M_1_led_4_10, D_und_M_1_led_4_11,
       D_und_M_1_led_5_2, D_und_M_1_led_5_5, D_und_M_1_led_5_7, D_und_M_1_led_5_9, D_und_M_1_led_5_11,
       D_und_M_1_led_6_2, D_und_M_1_led_6_5, D_und_M_1_led_6_7, D_und_M_1_led_6_11, D_und_M_1_led_7_2,
       D_und_M_1_led_7_4, D_und_M_1_led_7_7, D_und_M_1_led_7_11, D_und_M_1_led_8_2, D_und_M_1_led_8_3,
       D_und_M_1_led_8_7, D_und_M_1_led_8_11, h_und_m_1_led_3_2, h_und_m_1_led_4_2, h_und_m_1_led_5_2,
       h_und_m_1_led_5_7, h_und_m_1_led_5_8, h_und_m_1_led_5_9, h_und_m_1_led_5_10, h_und_m_1_led_5_11,
       h_und_m_1_led_6_2, h_und_m_1_led_6_3, h_und_m_1_led_6_4, h_und_m_1_led_6_5, h_und_m_1_led_6_7,
       h_und_m_1_led_6_9, h_und_m_1_led_6_11, h_und_m_1_led_7_2, h_und_m_1_led_7_5, h_und_m_1_led_7_7,
       h_und_m_1_led_7_9, h_und_m_1_led_7_11, h_und_m_1_led_8_2, h_und_m_1_led_8_5, h_und_m_1_led_8_7,
       h_und_m_1_led_8_11, m_und_s_1_led_4_8, m_und_s_1_led_4_9, m_und_s_1_led_4_10, m_und_s_1_led_5_2,
       m_und_s_1_led_5_3, m_und_s_1_led_5_4, m_und_s_1_led_5_5, m_und_s_1_led_5_6, m_und_s_1_led_5_8,
       m_und_s_1_led_6_2, m_und_s_1_led_6_4, m_und_s_1_led_6_6, m_und_s_1_led_6_8, m_und_s_1_led_6_9,
       m_und_s_1_led_6_10, m_und_s_1_led_7_2, m_und_s_1_led_7_4, m_und_s_1_led_7_6, m_und_s_1_led_7_10,
       m_und_s_1_led_8_2, m_und_s_1_led_8_6, m_und_s_1_led_8_8, m_und_s_1_led_8_9, m_und_s_1_led_8_10,
       or_1_out, or_2_out, or_3_out, or_4_out, or_5_out, or_6_out, or_7_out, or_8_out, or_9_out, or_10_out,
       or_11_out, or_12_out, or_13_out, or_14_out, or_15_out, or_16_out, or_17_out, or_18_out, or_19_out,
       or_20_out, or_21_out, or_22_out, or_23_out, or_24_out, or_25_out, or_26_out, or_27_out, or_28_out,
       or_29_out, or_30_out, Y_1_led_3_7, Y_1_led_3_11, Y_1_led_4_7, Y_1_led_4_11, Y_1_led_5_8, Y_1_led_5_10,
       Y_1_led_6_9, Y_1_led_7_9, Y_1_led_8_9;

  and and_1 (LED_Rahmen_Rest_Wecker, Takt_blinken, Weckfunktion_Ein);
  h_und_m h_und_m_1 (
    .Taste_min_sek(Eingangstaste_Min_Sek), .Taste_tag_mon(Eingangstaste_Tag_Monat),
    .Taste_jahr(Eingangstaste_Jahr), .LED_3_2(h_und_m_1_led_3_2), .LED_4_2(h_und_m_1_led_4_2),
    .LED_5_2(h_und_m_1_led_5_2), .LED_5_7(h_und_m_1_led_5_7), .LED_5_8(h_und_m_1_led_5_8),
    .LED_5_9(h_und_m_1_led_5_9), .LED_5_10(h_und_m_1_led_5_10), .LED_5_11(h_und_m_1_led_5_11),
    .LED_6_2(h_und_m_1_led_6_2), .LED_6_3(h_und_m_1_led_6_3), .LED_6_4(h_und_m_1_led_6_4),
    .LED_6_5(h_und_m_1_led_6_5), .LED_6_7(h_und_m_1_led_6_7), .LED_6_9(h_und_m_1_led_6_9),
    .LED_6_11(h_und_m_1_led_6_11), .LED_7_2(h_und_m_1_led_7_2), .LED_7_5(h_und_m_1_led_7_5),
    .LED_7_7(h_und_m_1_led_7_7), .LED_7_9(h_und_m_1_led_7_9), .LED_7_11(h_und_m_1_led_7_11),
    .LED_8_2(h_und_m_1_led_8_2), .LED_8_5(h_und_m_1_led_8_5), .LED_8_7(h_und_m_1_led_8_7),
    .LED_8_11(h_und_m_1_led_8_11));
  m_und_s m_und_s_1 (
    .Taste_min_sek(Eingangstaste_Min_Sek), .LED_4_8(m_und_s_1_led_4_8), .LED_4_9(m_und_s_1_led_4_9),
    .LED_4_10(m_und_s_1_led_4_10), .LED_5_2(m_und_s_1_led_5_2), .LED_5_3(m_und_s_1_led_5_3),
    .LED_5_4(m_und_s_1_led_5_4), .LED_5_5(m_und_s_1_led_5_5), .LED_5_6(m_und_s_1_led_5_6),
    .LED_5_8(m_und_s_1_led_5_8), .LED_6_2(m_und_s_1_led_6_2), .LED_6_4(m_und_s_1_led_6_4),
    .LED_6_6(m_und_s_1_led_6_6), .LED_6_8(m_und_s_1_led_6_8), .LED_6_9(m_und_s_1_led_6_9),
    .LED_6_10(m_und_s_1_led_6_10), .LED_7_2(m_und_s_1_led_7_2), .LED_7_4(m_und_s_1_led_7_4),
    .LED_7_6(m_und_s_1_led_7_6), .LED_7_10(m_und_s_1_led_7_10), .LED_8_2(m_und_s_1_led_8_2),
    .LED_8_6(m_und_s_1_led_8_6), .LED_8_8(m_und_s_1_led_8_8), .LED_8_9(m_und_s_1_led_8_9),
    .LED_8_10(m_und_s_1_led_8_10));
  D_und_M D_und_M_1 (
    .Taste_Tag_Monat(Eingangstaste_Tag_Monat), .LED_3_2(D_und_M_1_led_3_2), .LED_3_3(D_und_M_1_led_3_3),
    .LED_3_7(D_und_M_1_led_3_7), .LED_3_11(D_und_M_1_led_3_11), .LED_4_2(D_und_M_1_led_4_2),
    .LED_4_4(D_und_M_1_led_4_4), .LED_4_7(D_und_M_1_led_4_7), .LED_4_8(D_und_M_1_led_4_8),
    .LED_4_10(D_und_M_1_led_4_10), .LED_4_11(D_und_M_1_led_4_11), .LED_5_2(D_und_M_1_led_5_2),
    .LED_5_5(D_und_M_1_led_5_5), .LED_5_7(D_und_M_1_led_5_7), .LED_5_9(D_und_M_1_led_5_9),
    .LED_5_11(D_und_M_1_led_5_11), .LED_6_2(D_und_M_1_led_6_2), .LED_6_5(D_und_M_1_led_6_5),
    .LED_6_7(D_und_M_1_led_6_7), .LED_6_11(D_und_M_1_led_6_11), .LED_7_2(D_und_M_1_led_7_2),
    .LED_7_4(D_und_M_1_led_7_4), .LED_7_7(D_und_M_1_led_7_7), .LED_7_11(D_und_M_1_led_7_11),
    .LED_8_2(D_und_M_1_led_8_2), .LED_8_3(D_und_M_1_led_8_3), .LED_8_7(D_und_M_1_led_8_7),
    .LED_8_11(D_und_M_1_led_8_11));
  Y Y_1 (
    .Taste_Jahr(Eingangstaste_Jahr), .LED_3_7(Y_1_led_3_7), .LED_3_11(Y_1_led_3_11), .LED_4_7(Y_1_led_4_7),
    .LED_4_11(Y_1_led_4_11), .LED_5_8(Y_1_led_5_8), .LED_5_10(Y_1_led_5_10), .LED_6_9(Y_1_led_6_9),
    .LED_7_9(Y_1_led_7_9), .LED_8_9(Y_1_led_8_9));
  or or_1 (or_1_out, h_und_m_1_led_3_2, D_und_M_1_led_3_2);
  or or_2 (or_2_out, D_und_M_1_led_3_7, Y_1_led_3_7);
  or or_3 (or_3_out, D_und_M_1_led_3_11, Y_1_led_3_11);
  or or_4 (or_4_out, h_und_m_1_led_4_2, D_und_M_1_led_4_2);
  or or_5 (or_5_out, D_und_M_1_led_4_7, Y_1_led_4_7);
  or or_6 (or_6_out, m_und_s_1_led_4_8, D_und_M_1_led_4_8);
  or or_7 (or_7_out, m_und_s_1_led_4_10, D_und_M_1_led_4_10);
  or or_8 (or_8_out, D_und_M_1_led_4_11, Y_1_led_4_11);
  or or_9 (or_9_out, h_und_m_1_led_5_2, D_und_M_1_led_5_2, m_und_s_1_led_5_2);
  or or_10 (or_10_out, m_und_s_1_led_5_5, D_und_M_1_led_5_5);
  or or_11 (or_11_out, h_und_m_1_led_5_7, D_und_M_1_led_5_7);
  or or_12 (or_12_out, h_und_m_1_led_5_8, m_und_s_1_led_5_8, Y_1_led_5_8);
  or or_13 (or_13_out, h_und_m_1_led_5_9, D_und_M_1_led_5_9);
  or or_14 (or_14_out, h_und_m_1_led_5_10, Y_1_led_5_10);
  or or_15 (or_15_out, h_und_m_1_led_5_11, D_und_M_1_led_5_11);
  or or_16 (or_16_out, h_und_m_1_led_6_2, m_und_s_1_led_6_2, D_und_M_1_led_6_2);
  or or_17 (or_17_out, h_und_m_1_led_6_4, m_und_s_1_led_6_4);
  or or_18 (or_18_out, h_und_m_1_led_6_5, D_und_M_1_led_6_5);
  or or_19 (or_19_out, h_und_m_1_led_6_7, D_und_M_1_led_6_7);
  or or_20 (or_20_out, h_und_m_1_led_6_9, Y_1_led_6_9, m_und_s_1_led_6_9);
  or or_21 (or_21_out, h_und_m_1_led_6_11, D_und_M_1_led_6_11);
  or or_22 (or_22_out, h_und_m_1_led_7_2, m_und_s_1_led_7_2, D_und_M_1_led_7_2);
  or or_23 (or_23_out, m_und_s_1_led_7_4, D_und_M_1_led_7_4);
  or or_24 (or_24_out, D_und_M_1_led_7_7, h_und_m_1_led_7_7);
  or or_25 (or_25_out, h_und_m_1_led_7_9, Y_1_led_7_9);
  or or_26 (or_26_out, h_und_m_1_led_7_11, D_und_M_1_led_7_11);
  or or_27 (or_27_out, h_und_m_1_led_8_2, m_und_s_1_led_8_2, D_und_M_1_led_8_2);
  or or_28 (or_28_out, h_und_m_1_led_8_7, D_und_M_1_led_8_7);
  or or_29 (or_29_out, m_und_s_1_led_8_9, Y_1_led_8_9);
  or or_30 (or_30_out, h_und_m_1_led_8_11, D_und_M_1_led_8_11);
  xor xor_1 (LED_3_2, LED_Rahmen_Rest_Wecker, or_1_out);
  xor xor_2 (LED_3_3, LED_Rahmen_Rest_Wecker, D_und_M_1_led_3_3);
  xor xor_3 (LED_3_7, LED_Rahmen_Rest_Wecker, or_2_out);
  xor xor_4 (LED_3_11, LED_Rahmen_Rest_Wecker, or_3_out);
  xor xor_5 (LED_4_2, LED_Rahmen_Rest_Wecker, or_4_out);
  xor xor_6 (LED_4_4, LED_Rahmen_Rest_Wecker, D_und_M_1_led_4_4);
  xor xor_7 (LED_4_7, LED_Rahmen_Rest_Wecker, or_5_out);
  xor xor_8 (LED_4_8, LED_Rahmen_Rest_Wecker, or_6_out);
  xor xor_9 (LED_4_9, LED_Rahmen_Rest_Wecker, m_und_s_1_led_4_9);
  xor xor_10 (LED_4_10, LED_Rahmen_Rest_Wecker, or_7_out);
  xor xor_11 (LED_4_11, LED_Rahmen_Rest_Wecker, or_8_out);
  xor xor_12 (LED_5_2, LED_Rahmen_Rest_Wecker, or_9_out);
  xor xor_13 (LED_5_3, LED_Rahmen_Rest_Wecker, m_und_s_1_led_5_3);
  xor xor_14 (LED_5_4, LED_Rahmen_Rest_Wecker, m_und_s_1_led_5_4);
  xor xor_15 (LED_5_5, LED_Rahmen_Rest_Wecker, or_10_out);
  xor xor_16 (LED_5_6, LED_Rahmen_Rest_Wecker, m_und_s_1_led_5_6);
  xor xor_17 (LED_5_7, LED_Rahmen_Rest_Wecker, or_11_out);
  xor xor_18 (LED_5_8, LED_Rahmen_Rest_Wecker, or_12_out);
  xor xor_19 (LED_5_9, LED_Rahmen_Rest_Wecker, or_13_out);
  xor xor_20 (LED_5_10, LED_Rahmen_Rest_Wecker, or_14_out);
  xor xor_21 (LED_5_11, LED_Rahmen_Rest_Wecker, or_15_out);
  xor xor_22 (LED_6_2, LED_Rahmen_Rest_Wecker, or_16_out);
  xor xor_23 (LED_6_3, LED_Rahmen_Rest_Wecker, h_und_m_1_led_6_3);
  xor xor_24 (LED_6_4, LED_Rahmen_Rest_Wecker, or_17_out);
  xor xor_25 (LED_6_5, LED_Rahmen_Rest_Wecker, or_18_out);
  xor xor_26 (LED_6_6, LED_Rahmen_Rest_Wecker, m_und_s_1_led_6_6);
  xor xor_27 (LED_6_7, LED_Rahmen_Rest_Wecker, or_19_out);
  xor xor_28 (LED_6_8, LED_Rahmen_Rest_Wecker, m_und_s_1_led_6_8);
  xor xor_29 (LED_6_9, LED_Rahmen_Rest_Wecker, or_20_out);
  xor xor_30 (LED_6_10, LED_Rahmen_Rest_Wecker, m_und_s_1_led_6_10);
  xor xor_31 (LED_6_11, LED_Rahmen_Rest_Wecker, or_21_out);
  xor xor_32 (LED_7_2, LED_Rahmen_Rest_Wecker, or_22_out);
  xor xor_33 (LED_7_4, LED_Rahmen_Rest_Wecker, or_23_out);
  xor xor_34 (LED_7_5, LED_Rahmen_Rest_Wecker, h_und_m_1_led_7_5);
  xor xor_35 (LED_7_6, LED_Rahmen_Rest_Wecker, m_und_s_1_led_7_6);
  xor xor_36 (LED_7_7, LED_Rahmen_Rest_Wecker, or_24_out);
  xor xor_37 (LED_7_9, LED_Rahmen_Rest_Wecker, or_25_out);
  xor xor_38 (LED_7_10, LED_Rahmen_Rest_Wecker, m_und_s_1_led_7_10);
  xor xor_39 (LED_7_11, LED_Rahmen_Rest_Wecker, or_26_out);
  xor xor_40 (LED_8_2, LED_Rahmen_Rest_Wecker, or_27_out);
  xor xor_41 (LED_8_3, LED_Rahmen_Rest_Wecker, D_und_M_1_led_8_3);
  xor xor_42 (LED_8_5, LED_Rahmen_Rest_Wecker, h_und_m_1_led_8_5);
  xor xor_43 (LED_8_6, LED_Rahmen_Rest_Wecker, m_und_s_1_led_8_6);
  xor xor_44 (LED_8_7, LED_Rahmen_Rest_Wecker, or_28_out);
  xor xor_45 (LED_8_8, LED_Rahmen_Rest_Wecker, m_und_s_1_led_8_8);
  xor xor_46 (LED_8_9, LED_Rahmen_Rest_Wecker, or_29_out);
  xor xor_47 (LED_8_10, LED_Rahmen_Rest_Wecker, m_und_s_1_led_8_10);
  xor xor_48 (LED_8_11, LED_Rahmen_Rest_Wecker, or_30_out);
endmodule

module Part_LED_7Seg_Buntr1 (
  input  Eingang,
  input  Eingang_1,
  input  Eingang_2,
  input  Eingang_3,
  input  Eingang_4,
  input  Eingang_5,
  input  [4:0] Eingang_6,
  input  [4:0] Eingang_7,
  input  [5:0] Eingang_8,
  input  [5:0] Eingang_9,
  input  [5:0] Eingang_10,
  input  [4:0] Eingang_11,
  input  [3:0] Eingang_12,
  input  [6:0] Eingang_13
);

  wire Haupt7seg_jahr_zu_led, Haupt7seg_min_sek_zu_led, Haupt7seg_reset_wecker_seg1,
       Haupt7seg_reset_wecker_seg2, Haupt7seg_reset_wecker_seg3_4, Haupt7seg_seg_1a, Haupt7seg_seg_1b,
       Haupt7seg_seg_1c, Haupt7seg_seg_1d, Haupt7seg_seg_1e, Haupt7seg_seg_1f, Haupt7seg_seg_1g,
       Haupt7seg_seg_2a, Haupt7seg_seg_2b, Haupt7seg_seg_2c, Haupt7seg_seg_2d, Haupt7seg_seg_2e,
       Haupt7seg_seg_2f, Haupt7seg_seg_2g, Haupt7seg_seg_3a, Haupt7seg_seg_3b, Haupt7seg_seg_3c,
       Haupt7seg_seg_3d, Haupt7seg_seg_3e, Haupt7seg_seg_3f, Haupt7seg_seg_3g, Haupt7seg_seg_4a,
       Haupt7seg_seg_4b, Haupt7seg_seg_4c, Haupt7seg_seg_4d, Haupt7seg_seg_4e, Haupt7seg_seg_4f,
       Haupt7seg_seg_4g, Haupt7seg_tag_mon_zu_led, Haupt7seg_weckerfunktion_zu_led, Hauptsch_led_3_2,
       Hauptsch_led_3_3, Hauptsch_led_3_7, Hauptsch_led_3_11, Hauptsch_led_4_2, Hauptsch_led_4_4,
       Hauptsch_led_4_7, Hauptsch_led_4_8, Hauptsch_led_4_9, Hauptsch_led_4_10, Hauptsch_led_4_11,
       Hauptsch_led_5_2, Hauptsch_led_5_3, Hauptsch_led_5_4, Hauptsch_led_5_5, Hauptsch_led_5_6,
       Hauptsch_led_5_7, Hauptsch_led_5_8, Hauptsch_led_5_9, Hauptsch_led_5_10, Hauptsch_led_5_11,
       Hauptsch_led_6_2, Hauptsch_led_6_3, Hauptsch_led_6_4, Hauptsch_led_6_5, Hauptsch_led_6_6,
       Hauptsch_led_6_7, Hauptsch_led_6_8, Hauptsch_led_6_9, Hauptsch_led_6_10, Hauptsch_led_6_11,
       Hauptsch_led_7_2, Hauptsch_led_7_4, Hauptsch_led_7_5, Hauptsch_led_7_6, Hauptsch_led_7_7,
       Hauptsch_led_7_9, Hauptsch_led_7_10, Hauptsch_led_7_11, Hauptsch_led_8_2, Hauptsch_led_8_3,
       Hauptsch_led_8_5, Hauptsch_led_8_6, Hauptsch_led_8_7, Hauptsch_led_8_8, Hauptsch_led_8_9,
       Hauptsch_led_8_10, Hauptsch_led_8_11, Hauptsch_led_rahmen_rest_wecker;

  _7_Segment_Display u_7_segment_display_1 (
    .g(Haupt7seg_seg_1g), .f(Haupt7seg_seg_1f), .a(Haupt7seg_seg_1a), .b(Haupt7seg_seg_1b),
    .e(Haupt7seg_seg_1e), .d(Haupt7seg_seg_1d), .c(Haupt7seg_seg_1c));  // open: dp
  _7_Segment_Display u_7_segment_display_2 (
    .g(Haupt7seg_seg_2g), .f(Haupt7seg_seg_2f), .a(Haupt7seg_seg_2a), .b(Haupt7seg_seg_2b),
    .e(Haupt7seg_seg_2e), .d(Haupt7seg_seg_2d), .c(Haupt7seg_seg_2c));  // open: dp
  _7_Segment_Display u_7_segment_display_3 (
    .g(Haupt7seg_seg_3g), .f(Haupt7seg_seg_3f), .a(Haupt7seg_seg_3a), .b(Haupt7seg_seg_3b),
    .e(Haupt7seg_seg_3e), .d(Haupt7seg_seg_3d), .c(Haupt7seg_seg_3c));  // open: dp
  _7_Segment_Display u_7_segment_display_4 (
    .g(Haupt7seg_seg_4g), .f(Haupt7seg_seg_4f), .a(Haupt7seg_seg_4a), .b(Haupt7seg_seg_4b),
    .e(Haupt7seg_seg_4e), .d(Haupt7seg_seg_4d), .c(Haupt7seg_seg_4c));  // open: dp
  Hauptschaltung_7Seg_Anzeige Haupt7seg (
    .Seg_2A(Haupt7seg_seg_2a), .Seg_1D(Haupt7seg_seg_1d), .Seg_2C(Haupt7seg_seg_2c),
    .Seg_1G(Haupt7seg_seg_1g), .Seg_1C(Haupt7seg_seg_1c), .Takt_Wecker_Stellen(Eingang),
    .Taste_Gecko_Tag_Mon(Eingang_2), .Schalter_Gecko_Wecker_Ein_Aus(Eingang_5), .Seg_2G(Haupt7seg_seg_2g),
    .Seg_2E(Haupt7seg_seg_2e), .Seg_2B(Haupt7seg_seg_2b), .Seg_2F(Haupt7seg_seg_2f),
    .Seg_2D(Haupt7seg_seg_2d), .Taste_Gecko_Jahr(Eingang_3), .Schalter_Gecko_Wecker_Stellem(Eingang_4),
    .Seg_1A(Haupt7seg_seg_1a), .Taste_Gecko_Min_Sek(Eingang_1), .Seg_1F(Haupt7seg_seg_1f),
    .Seg_1E(Haupt7seg_seg_1e), .Seg_1B(Haupt7seg_seg_1b), .Seg_3A(Haupt7seg_seg_3a),
    .Seg_3B(Haupt7seg_seg_3b), .Seg_3C(Haupt7seg_seg_3c), .Seg_3D(Haupt7seg_seg_3d),
    .Seg_3E(Haupt7seg_seg_3e), .Seg_3F(Haupt7seg_seg_3f), .Seg_3G(Haupt7seg_seg_3g),
    .Seg_4A(Haupt7seg_seg_4a), .Seg_4B(Haupt7seg_seg_4b), .Seg_4C(Haupt7seg_seg_4c),
    .Seg_4D(Haupt7seg_seg_4d), .Seg_4E(Haupt7seg_seg_4e), .Seg_4F(Haupt7seg_seg_4f),
    .Seg_4G(Haupt7seg_seg_4g), .Weckerfunktion_zu_LED(Haupt7seg_weckerfunktion_zu_led),
    .Min_sek_zu_LED(Haupt7seg_min_sek_zu_led), .Tag_Mon_zu_LED(Haupt7seg_tag_mon_zu_led),
    .Jahr_zu_LED(Haupt7seg_jahr_zu_led), .Stundenbits(Eingang_6), .Wecker_Stundenbits(Eingang_7),
    .Minutenbits(Eingang_8), .Wecker_Minutenbits(Eingang_9), .Sekundenbits(Eingang_10),
    .Jahrbits(Eingang_13), .Tagbits(Eingang_11), .Monatbits(Eingang_12),
    .Reset_Wecker_Seg1(Haupt7seg_reset_wecker_seg1), .Reset_Wecker_Seg3_4(Haupt7seg_reset_wecker_seg3_4),
    .Reset_Wecker_Seg2(Haupt7seg_reset_wecker_seg2));
  LED led_1 (.in(Hauptsch_led_rahmen_rest_wecker));
  LED led_2 (.in(Hauptsch_led_rahmen_rest_wecker));
  LED led_3 (.in(Hauptsch_led_rahmen_rest_wecker));
  LED led_4 (.in(Hauptsch_led_rahmen_rest_wecker));
  LED led_5 (.in(Hauptsch_led_rahmen_rest_wecker));
  LED led_6 (.in(Hauptsch_led_rahmen_rest_wecker));
  LED led_7 (.in(Hauptsch_led_rahmen_rest_wecker));
  LED led_8 (.in(Hauptsch_led_rahmen_rest_wecker));
  LED led_9 (.in(Hauptsch_led_rahmen_rest_wecker));
  LED led_10 (.in(Hauptsch_led_rahmen_rest_wecker));
  LED led_11 (.in(Hauptsch_led_rahmen_rest_wecker));
  LED led_12 (.in(Hauptsch_led_rahmen_rest_wecker));
  LED led_13 (.in(Hauptsch_led_rahmen_rest_wecker));
  LED led_14 (.in(Hauptsch_led_rahmen_rest_wecker));
  LED led_15 (.in(Hauptsch_led_3_3));
  LED led_16 (.in(Hauptsch_led_3_2));
  LED led_17 (.in(Hauptsch_led_rahmen_rest_wecker));
  LED led_18 (.in(Hauptsch_led_4_2));
  LED led_19 (.in(Hauptsch_led_5_3));
  LED led_20 (.in(Hauptsch_led_5_2));
  LED led_21 (.in(Hauptsch_led_6_3));
  LED led_22 (.in(Hauptsch_led_6_2));
  LED led_23 (.in(Hauptsch_led_rahmen_rest_wecker));
  LED led_24 (.in(Hauptsch_led_7_2));
  LED led_25 (.in(Hauptsch_led_8_2));
  LED led_26 (.in(Hauptsch_led_8_3));
  LED led_27 (.in(Hauptsch_led_rahmen_rest_wecker));
  LED led_28 (.in(Hauptsch_led_rahmen_rest_wecker));
  LED led_29 (.in(Hauptsch_led_rahmen_rest_wecker));
  LED led_30 (.in(Hauptsch_led_rahmen_rest_wecker));
  LED led_31 (.in(Hauptsch_led_rahmen_rest_wecker));
  LED led_32 (.in(Hauptsch_led_rahmen_rest_wecker));
  LED led_33 (.in(Hauptsch_led_rahmen_rest_wecker));
  LED led_34 (.in(Hauptsch_led_rahmen_rest_wecker));
  LED led_35 (.in(Hauptsch_led_rahmen_rest_wecker));
  LED led_36 (.in(Hauptsch_led_rahmen_rest_wecker));
  LED led_37 (.in(Hauptsch_led_4_4));
  LED led_38 (.in(Hauptsch_led_rahmen_rest_wecker));
  LED led_39 (.in(Hauptsch_led_5_5));
  LED led_40 (.in(Hauptsch_led_5_4));
  LED led_41 (.in(Hauptsch_led_6_5));
  LED led_42 (.in(Hauptsch_led_6_4));
  LED led_43 (.in(Hauptsch_led_7_4));
  LED led_44 (.in(Hauptsch_led_7_5));
  LED led_45 (.in(Hauptsch_led_rahmen_rest_wecker));
  LED led_46 (.in(Hauptsch_led_8_5));
  LED led_47 (.in(Hauptsch_led_rahmen_rest_wecker));
  LED led_48 (.in(Hauptsch_led_rahmen_rest_wecker));
  LED led_49 (.in(Hauptsch_led_rahmen_rest_wecker));
  LED led_50 (.in(Hauptsch_led_rahmen_rest_wecker));
  LED led_51 (.in(Hauptsch_led_rahmen_rest_wecker));
  LED led_52 (.in(Hauptsch_led_rahmen_rest_wecker));
  LED led_53 (.in(Hauptsch_led_rahmen_rest_wecker));
  LED led_54 (.in(Hauptsch_led_rahmen_rest_wecker));
  LED led_55 (.in(Hauptsch_led_rahmen_rest_wecker));
  LED led_56 (.in(Hauptsch_led_3_7));
  LED led_57 (.in(Hauptsch_led_rahmen_rest_wecker));
  LED led_58 (.in(Hauptsch_led_4_7));
  LED led_59 (.in(Hauptsch_led_5_7));
  LED led_60 (.in(Hauptsch_led_5_6));
  LED led_61 (.in(Hauptsch_led_6_7));
  LED led_62 (.in(Hauptsch_led_6_6));
  LED led_63 (.in(Hauptsch_led_7_6));
  LED led_64 (.in(Hauptsch_led_7_7));
  LED led_65 (.in(Hauptsch_led_8_7));
  LED led_66 (.in(Hauptsch_led_8_6));
  LED led_67 (.in(Hauptsch_led_rahmen_rest_wecker));
  LED led_68 (.in(Hauptsch_led_rahmen_rest_wecker));
  LED led_69 (.in(Hauptsch_led_rahmen_rest_wecker));
  LED led_70 (.in(Hauptsch_led_rahmen_rest_wecker));
  LED led_71 (.in(Hauptsch_led_rahmen_rest_wecker));
  LED led_72 (.in(Hauptsch_led_rahmen_rest_wecker));
  LED led_73 (.in(Hauptsch_led_rahmen_rest_wecker));
  LED led_74 (.in(Hauptsch_led_rahmen_rest_wecker));
  LED led_75 (.in(Hauptsch_led_rahmen_rest_wecker));
  LED led_76 (.in(Hauptsch_led_rahmen_rest_wecker));
  LED led_77 (.in(Hauptsch_led_4_9));
  LED led_78 (.in(Hauptsch_led_4_8));
  LED led_79 (.in(Hauptsch_led_5_9));
  LED led_80 (.in(Hauptsch_led_5_8));
  LED led_81 (.in(Hauptsch_led_6_8));
  LED led_82 (.in(Hauptsch_led_6_9));
  LED led_83 (.in(Hauptsch_led_rahmen_rest_wecker));
  LED led_84 (.in(Hauptsch_led_7_9));
  LED led_85 (.in(Hauptsch_led_8_8));
  LED led_86 (.in(Hauptsch_led_8_9));
  LED led_87 (.in(Hauptsch_led_rahmen_rest_wecker));
  LED led_88 (.in(Hauptsch_led_rahmen_rest_wecker));
  LED led_89 (.in(Hauptsch_led_rahmen_rest_wecker));
  LED led_90 (.in(Hauptsch_led_rahmen_rest_wecker));
  LED led_91 (.in(Hauptsch_led_rahmen_rest_wecker));
  LED led_92 (.in(Hauptsch_led_rahmen_rest_wecker));
  LED led_93 (.in(Hauptsch_led_rahmen_rest_wecker));
  LED led_94 (.in(Hauptsch_led_rahmen_rest_wecker));
  LED led_95 (.in(Hauptsch_led_rahmen_rest_wecker));
  LED led_96 (.in(Hauptsch_led_3_11));
  LED led_97 (.in(Hauptsch_led_4_11));
  LED led_98 (.in(Hauptsch_led_4_10));
  LED led_99 (.in(Hauptsch_led_5_10));
  LED led_100 (.in(Hauptsch_led_5_11));
  LED led_101 (.in(Hauptsch_led_6_11));
  LED led_102 (.in(Hauptsch_led_6_10));
  LED led_103 (.in(Hauptsch_led_7_10));
  LED led_104 (.in(Hauptsch_led_7_11));
  LED led_105 (.in(Hauptsch_led_8_10));
  LED led_106 (.in(Hauptsch_led_8_11));
  LED led_107 (.in(Hauptsch_led_rahmen_rest_wecker));
  LED led_108 (.in(Hauptsch_led_rahmen_rest_wecker));
  LED led_109 (.in(Hauptsch_led_rahmen_rest_wecker));
  LED led_110 (.in(Hauptsch_led_rahmen_rest_wecker));
  Hauptschaltung_LED_Anzeige Hauptsch (
    .LED_6_11(Hauptsch_led_6_11), .LED_6_10(Hauptsch_led_6_10), .LED_6_9(Hauptsch_led_6_9),
    .LED_6_8(Hauptsch_led_6_8), .LED_6_7(Hauptsch_led_6_7), .LED_6_6(Hauptsch_led_6_6),
    .LED_6_5(Hauptsch_led_6_5), .LED_6_4(Hauptsch_led_6_4), .LED_6_3(Hauptsch_led_6_3),
    .LED_6_2(Hauptsch_led_6_2), .LED_5_11(Hauptsch_led_5_11), .LED_5_10(Hauptsch_led_5_10),
    .LED_5_9(Hauptsch_led_5_9), .LED_5_8(Hauptsch_led_5_8), .LED_5_7(Hauptsch_led_5_7),
    .LED_5_6(Hauptsch_led_5_6), .LED_5_5(Hauptsch_led_5_5), .LED_5_4(Hauptsch_led_5_4),
    .LED_5_3(Hauptsch_led_5_3), .LED_5_2(Hauptsch_led_5_2), .LED_4_11(Hauptsch_led_4_11),
    .LED_4_10(Hauptsch_led_4_10), .LED_4_9(Hauptsch_led_4_9), .LED_4_8(Hauptsch_led_4_8),
    .LED_4_7(Hauptsch_led_4_7), .LED_4_4(Hauptsch_led_4_4), .LED_4_2(Hauptsch_led_4_2),
    .LED_3_11(Hauptsch_led_3_11), .LED_3_7(Hauptsch_led_3_7), .LED_3_3(Hauptsch_led_3_3),
    .LED_3_2(Hauptsch_led_3_2), .LED_Rahmen_Rest_Wecker(Hauptsch_led_rahmen_rest_wecker),
    .Eingangstaste_Jahr(Haupt7seg_jahr_zu_led), .Eingangstaste_Tag_Monat(Haupt7seg_tag_mon_zu_led),
    .Eingangstaste_Min_Sek(Haupt7seg_min_sek_zu_led), .Weckfunktion_Ein(Haupt7seg_weckerfunktion_zu_led),
    .Takt_blinken(Eingang), .LED_7_2(Hauptsch_led_7_2), .LED_7_4(Hauptsch_led_7_4),
    .LED_7_5(Hauptsch_led_7_5), .LED_7_6(Hauptsch_led_7_6), .LED_7_7(Hauptsch_led_7_7),
    .LED_7_9(Hauptsch_led_7_9), .LED_7_10(Hauptsch_led_7_10), .LED_7_11(Hauptsch_led_7_11),
    .LED_8_2(Hauptsch_led_8_2), .LED_8_3(Hauptsch_led_8_3), .LED_8_5(Hauptsch_led_8_5),
    .LED_8_6(Hauptsch_led_8_6), .LED_8_7(Hauptsch_led_8_7), .LED_8_8(Hauptsch_led_8_8),
    .LED_8_9(Hauptsch_led_8_9), .LED_8_10(Hauptsch_led_8_10), .LED_8_11(Hauptsch_led_8_11));
  LED led_111 (.in(Hauptsch_led_rahmen_rest_wecker));
  LED led_112 (.in(Hauptsch_led_rahmen_rest_wecker));
  LED led_113 (.in(Hauptsch_led_rahmen_rest_wecker));
  LED led_114 (.in(Hauptsch_led_rahmen_rest_wecker));
  LED led_115 (.in(Hauptsch_led_rahmen_rest_wecker));
  LED led_116 (.in(Hauptsch_led_rahmen_rest_wecker));
  LED led_117 (.in(Hauptsch_led_rahmen_rest_wecker));
  LED led_118 (.in(Hauptsch_led_rahmen_rest_wecker));
  LED led_119 (.in(Hauptsch_led_rahmen_rest_wecker));
  LED led_120 (.in(Hauptsch_led_rahmen_rest_wecker));
endmodule

module h_und_m (
  input  Taste_min_sek,
  input  Taste_tag_mon,
  input  Taste_jahr,
  output LED_3_2,
  output LED_4_2,
  output LED_5_2,
  output LED_5_7,
  output LED_5_8,
  output LED_5_9,
  output LED_5_10,
  output LED_5_11,
  output LED_6_2,
  output LED_6_3,
  output LED_6_4,
  output LED_6_5,
  output LED_6_7,
  output LED_6_9,
  output LED_6_11,
  output LED_7_2,
  output LED_7_5,
  output LED_7_7,
  output LED_7_9,
  output LED_7_11,
  output LED_8_2,
  output LED_8_5,
  output LED_8_7,
  output LED_8_11
);

  and and_1 (LED_3_2, ~Taste_min_sek, ~Taste_tag_mon, ~Taste_jahr);  // AND_Gate

  assign LED_4_2 = LED_3_2;
  assign LED_5_2 = LED_3_2;
  assign LED_5_7 = LED_3_2;
  assign LED_5_8 = LED_3_2;
  assign LED_5_9 = LED_3_2;
  assign LED_5_10 = LED_3_2;
  assign LED_5_11 = LED_3_2;
  assign LED_6_2 = LED_3_2;
  assign LED_6_3 = LED_3_2;
  assign LED_6_4 = LED_3_2;
  assign LED_6_5 = LED_3_2;
  assign LED_6_7 = LED_3_2;
  assign LED_6_9 = LED_3_2;
  assign LED_6_11 = LED_3_2;
  assign LED_7_2 = LED_3_2;
  assign LED_7_5 = LED_3_2;
  assign LED_7_7 = LED_3_2;
  assign LED_7_9 = LED_3_2;
  assign LED_7_11 = LED_3_2;
  assign LED_8_2 = LED_3_2;
  assign LED_8_5 = LED_3_2;
  assign LED_8_7 = LED_3_2;
  assign LED_8_11 = LED_3_2;
endmodule

module m_und_s (
  input  Taste_min_sek,
  output LED_4_8,
  output LED_4_9,
  output LED_4_10,
  output LED_5_2,
  output LED_5_3,
  output LED_5_4,
  output LED_5_5,
  output LED_5_6,
  output LED_5_8,
  output LED_6_2,
  output LED_6_4,
  output LED_6_6,
  output LED_6_8,
  output LED_6_9,
  output LED_6_10,
  output LED_7_2,
  output LED_7_4,
  output LED_7_6,
  output LED_7_10,
  output LED_8_2,
  output LED_8_6,
  output LED_8_8,
  output LED_8_9,
  output LED_8_10
);


  assign LED_4_8 = Taste_min_sek;
  assign LED_4_9 = Taste_min_sek;
  assign LED_4_10 = Taste_min_sek;
  assign LED_5_2 = Taste_min_sek;
  assign LED_5_3 = Taste_min_sek;
  assign LED_5_4 = Taste_min_sek;
  assign LED_5_5 = Taste_min_sek;
  assign LED_5_6 = Taste_min_sek;
  assign LED_5_8 = Taste_min_sek;
  assign LED_6_2 = Taste_min_sek;
  assign LED_6_4 = Taste_min_sek;
  assign LED_6_6 = Taste_min_sek;
  assign LED_6_8 = Taste_min_sek;
  assign LED_6_9 = Taste_min_sek;
  assign LED_6_10 = Taste_min_sek;
  assign LED_7_2 = Taste_min_sek;
  assign LED_7_4 = Taste_min_sek;
  assign LED_7_6 = Taste_min_sek;
  assign LED_7_10 = Taste_min_sek;
  assign LED_8_2 = Taste_min_sek;
  assign LED_8_6 = Taste_min_sek;
  assign LED_8_8 = Taste_min_sek;
  assign LED_8_9 = Taste_min_sek;
  assign LED_8_10 = Taste_min_sek;
endmodule

module D_und_M (
  input  Taste_Tag_Monat,
  output LED_3_2,
  output LED_3_3,
  output LED_3_7,
  output LED_3_11,
  output LED_4_2,
  output LED_4_4,
  output LED_4_7,
  output LED_4_8,
  output LED_4_10,
  output LED_4_11,
  output LED_5_2,
  output LED_5_5,
  output LED_5_7,
  output LED_5_9,
  output LED_5_11,
  output LED_6_2,
  output LED_6_5,
  output LED_6_7,
  output LED_6_11,
  output LED_7_2,
  output LED_7_4,
  output LED_7_7,
  output LED_7_11,
  output LED_8_2,
  output LED_8_3,
  output LED_8_7,
  output LED_8_11
);


  assign LED_3_2 = Taste_Tag_Monat;
  assign LED_3_3 = Taste_Tag_Monat;
  assign LED_3_7 = Taste_Tag_Monat;
  assign LED_3_11 = Taste_Tag_Monat;
  assign LED_4_2 = Taste_Tag_Monat;
  assign LED_4_4 = Taste_Tag_Monat;
  assign LED_4_7 = Taste_Tag_Monat;
  assign LED_4_8 = Taste_Tag_Monat;
  assign LED_4_10 = Taste_Tag_Monat;
  assign LED_4_11 = Taste_Tag_Monat;
  assign LED_5_2 = Taste_Tag_Monat;
  assign LED_5_5 = Taste_Tag_Monat;
  assign LED_5_7 = Taste_Tag_Monat;
  assign LED_5_9 = Taste_Tag_Monat;
  assign LED_5_11 = Taste_Tag_Monat;
  assign LED_6_2 = Taste_Tag_Monat;
  assign LED_6_5 = Taste_Tag_Monat;
  assign LED_6_7 = Taste_Tag_Monat;
  assign LED_6_11 = Taste_Tag_Monat;
  assign LED_7_2 = Taste_Tag_Monat;
  assign LED_7_4 = Taste_Tag_Monat;
  assign LED_7_7 = Taste_Tag_Monat;
  assign LED_7_11 = Taste_Tag_Monat;
  assign LED_8_2 = Taste_Tag_Monat;
  assign LED_8_3 = Taste_Tag_Monat;
  assign LED_8_7 = Taste_Tag_Monat;
  assign LED_8_11 = Taste_Tag_Monat;
endmodule

module Y (
  input  Taste_Jahr,
  output LED_3_7,
  output LED_3_11,
  output LED_4_7,
  output LED_4_11,
  output LED_5_8,
  output LED_5_10,
  output LED_6_9,
  output LED_7_9,
  output LED_8_9
);


  assign LED_3_7 = Taste_Jahr;
  assign LED_3_11 = Taste_Jahr;
  assign LED_4_7 = Taste_Jahr;
  assign LED_4_11 = Taste_Jahr;
  assign LED_5_8 = Taste_Jahr;
  assign LED_5_10 = Taste_Jahr;
  assign LED_6_9 = Taste_Jahr;
  assign LED_7_9 = Taste_Jahr;
  assign LED_8_9 = Taste_Jahr;
endmodule
