// Logisim project LED_und_7Seg_Anzeige_Final.circ as structural Verilog: 10 circuits, main circuit Part_Buntr1_Final
module Hauptschaltung_LED_Anzeige (
  input  Input_1,
  input  Weckfunktion,
  input  Eingangstaste_Min_Sek,
  input  Eingangstaste_Tag_Monat,
  input  Eingangstaste_Jahr,
  output LED_Rahmen_Rest_Wecker,
  output LED_3_2,
  output LED_3_3,
  output LED_3_7,
  output LED_3_11,
  output LED_4_2,
  output LED_4_4,
  output LED_4_7,
  output LED_4_8,
  output LED_4_9,
  output LED_4_10,
  output LED_4_11,
  output LED_5_2,
  output LED_5_3,
  output LED_5_4,
  output LED_5_5,
  output LED_5_6,
  output LED_5_7,
  output LED_5_8,
  output LED_5_9,
  output LED_5_10,
  output LED_5_11,
  output LED_6_2,
  output LED_6_3,
  output LED_6_4,
  output LED_6_5,
  output LED_6_6,
  output LED_6_7,
  output LED_6_8,
  output LED_6_9,
  output LED_6_10,
  output LED_6_11,
  output LED_7_2,
  output LED_7_4,
  output LED_7_5,
  output LED_7_6,
  output LED_7_7,
  output LED_7_9,
  output LED_7_10,
  output LED_7_11,
  output LED_8_2,
  output LED_8_3,
  output LED_8_5,
  output LED_8_6,
  output LED_8_7,
  output LED_8_8,
  output LED_8_9,
  output LED_8_10,
  output LED_8_11
);

  wire D_und_M_1_led_3_2, D_und_M_1_led_3_3, D_und_M_1_led_3_7, D_und_M_1_led_3_11, D_und_M_1_led_4_2,
       D_und_M_1_led_4_4, D_und_M_1_led_4_7, D_und_M_1_led_4_8, D_und_M_1_led_4_10, D_und_M_1_led_4_11,
       D_und_M_1_led_5_2, D_und_M_1_led_5_5, D_und_M_1_led_5_7, D_und_M_1_led_5_9, D_und_M_1_led_5_11,
       D_und_M_1_led_6_2, D_und_M_1_led_6_5, D_und_M_1_led_6_7, D_und_M_1_led_6_11, D_und_M_1_led_7_2,
       D_und_M_1_led_7_4, D_und_M_1_led_7_7, D_und_M_1_led_7_11, D_und_M_1_led_8_2, D_und_M_1_led_8_3,
       D_und_M_1_led_8_7, D_und_M_1_led_8_11, h_und_m_1_led_3_2, h_und_m_1_led_4_2, h_und_m_1_led_5_2,
       h_und_m_1_led_5_7, h_und_m_1_led_5_8, h_und_m_1_led_5_9, h_und_m_1_led_5_10, h_und_m_1_led_5_11,
       h_und_m_1_led_6_2, h_und_m_1_led_6_3, h_und_m_1_led_6_4, h_und_m_1_led_6_5, h_und_m_1_led_6_7,
       h_und_m_1_led_6_9, h_und_m_1_led_6_11, h_und_m_1_led_7_2, h_und_m_1_led_7_5, h_und_m_1_led_7_7,
       h_und_m_1_led_7_9, h_und_m_1_led_7_11, h_und_m_1_led_8_2, h_und_m_1_led_8_5, h_und_m_1_led_8_7,
       h_und_m_1_led_8_11, m_und_s_1_led_4_8, m_und_s_1_led_4_9, m_und_s_1_led_4_10, m_und_s_1_led_5_2,
       m_und_s_1_led_5_3, m_und_s_1_led_5_4, m_und_s_1_led_5_5, m_und_s_1_led_5_6, m_und_s_1_led_5_8,
       m_und_s_1_led_6_2, m_und_s_1_led_6_4, m_und_s_1_led_6_6, m_und_s_1_led_6_8, m_und_s_1_led_6_9,
       m_und_s_1_led_6_10, m_und_s_1_led_7_2, m_und_s_1_led_7_4, m_und_s_1_led_7_6, m_und_s_1_led_7_10,
       m_und_s_1_led_8_2, m_und_s_1_led_8_6, m_und_s_1_led_8_8, m_und_s_1_led_8_9, m_und_s_1_led_8_10,
       or_1_out, or_2_out, or_3_out, or_4_out, or_5_out, or_6_out, or_7_out, or_8_out, or_9_out, or_10_out,
       or_11_out, or_12_out, or_13_out, or_14_out, or_15_out, or_16_out, or_17_out, or_18_out, or_19_out,
       or_20_out, or_21_out, or_22_out, or_23_out, or_24_out, or_25_out, or_26_out, or_27_out, or_28_out,
       or_29_out, or_30_out, Y_1_led_3_7, Y_1_led_3_11, Y_1_led_4_7, Y_1_led_4_11, Y_1_led_5_8, Y_1_led_5_10,
       Y_1_led_6_9, Y_1_led_7_9, Y_1_led_8_9;

  and and_1 (LED_Rahmen_Rest_Wecker, Input_1, Weckfunktion);
  h_und_m h_und_m_1 (
    .Taste_min_sek(Eingangstaste_Min_Sek), .Taste_tag_mon(Eingangstaste_Tag_Monat),
    .Taste_jahr(Eingangstaste_Jahr), .LED_3_2(h_und_m_1_led_3_2), .LED_4_2(h_und_m_1_led_4_2),
    .LED_5_2(h_und_m_1_led_5_2), .LED_5_7(h_und_m_1_led_5_7), .LED_5_8(h_und_m_1_led_5_8),
    .LED_5_9(h_und_m_1_led_5_9), .LED_5_10(h_und_m_1_led_5_10), .LED_5_11(h_und_m_1_led_5_11),
    .LED_6_2(h_und_m_1_led_6_2), .LED_6_3(h_und_m_1_led_6_3), .LED_6_4(h_und_m_1_led_6_4),
    .LED_6_5(h_und_m_1_led_6_5), .LED_6_7(h_und_m_1_led_6_7), .LED_6_9(h_und_m_1_led_6_9),
    .LED_6_11(h_und_m_1_led_6_11), .LED_7_2(h_und_m_1_led_7_2), .LED_7_5(h_und_m_1_led_7_5),
    .LED_7_7(h_und_m_1_led_7_7), .LED_7_9(h_und_m_1_led_7_9), .LED_7_11(h_und_m_1_led_7_11),
    .LED_8_2(h_und_m_1_led_8_2), .LED_8_5(h_und_m_1_led_8_5), .LED_8_7(h_und_m_1_led_8_7),
    .LED_8_11(h_und_m_1_led_8_11));
  m_und_s m_und_s_1 (
    .Taste_min_sek(Eingangstaste_Min_Sek), .LED_4_8(m_und_s_1_led_4_8), .LED_4_9(m_und_s_1_led_4_9),
    .LED_4_10(m_und_s_1_led_4_10), .LED_5_2(m_und_s_1_led_5_2), .LED_5_3(m_und_s_1_led_5_3),
    .LED_5_4(m_und_s_1_led_5_4), .LED_5_5(m_und_s_1_led_5_5), .LED_5_6(m_und_s_1_led_5_6),
    .LED_5_8(m_und_s_1_led_5_8), .LED_6_2(m_und_s_1_led_6_2), .LED_6_4(m_und_s_1_led_6_4),
    .LED_6_6(m_und_s_1_led_6_6), .LED_6_8(m_und_s_1_led_6_8), .LED_6_9(m_und_s_1_led_6_9),
    .LED_6_10(m_und_s_1_led_6_10), .LED_7_2(m_und_s_1_led_7_2), .LED_7_4(m_und_s_1_led_7_4),
    .LED_7_6(m_und_s_1_led_7_6), .LED_7_10(m_und_s_1_led_7_10), .LED_8_2(m_und_s_1_led_8_2),
    .LED_8_6(m_und_s_1_led_8_6), .LED_8_8(m_und_s_1_led_8_8), .LED_8_9(m_und_s_1_led_8_9),
    .LED_8_10(m_und_s_1_led_8_10));
  D_und_M D_und_M_1 (
    .Taste_Tag_Monat(Eingangstaste_Tag_Monat), .LED_3_2(D_und_M_1_led_3_2), .LED_3_3(D_und_M_1_led_3_3),
    .LED_3_7(D_und_M_1_led_3_7), .LED_3_11(D_und_M_1_led_3_11), .LED_4_2(D_und_M_1_led_4_2),
    .LED_4_4(D_und_M_1_led_4_4), .LED_4_7(D_und_M_1_led_4_7), .LED_4_8(D_und_M_1_led_4_8),
    .LED_4_10(D_und_M_1_led_4_10), .LED_4_11(D_und_M_1_led_4_11), .LED_5_2(D_und_M_1_led_5_2),
    .LED_5_5(D_und_M_1_led_5_5), .LED_5_7(D_und_M_1_led_5_7), .LED_5_9(D_und_M_1_led_5_9),
    .LED_5_11(D_und_M_1_led_5_11), .LED_6_2(D_und_M_1_led_6_2), .LED_6_5(D_und_M_1_led_6_5),
    .LED_6_7(D_und_M_1_led_6_7), .LED_6_11(D_und_M_1_led_6_11), .LED_7_2(D_und_M_1_led_7_2),
    .LED_7_4(D_und_M_1_led_7_4), .LED_7_7(D_und_M_1_led_7_7), .LED_7_11(D_und_M_1_led_7_11),
    .LED_8_2(D_und_M_1_led_8_2), .LED_8_3(D_und_M_1_led_8_3), .LED_8_7(D_und_M_1_led_8_7),
    .LED_8_11(D_und_M_1_led_8_11));
  Y Y_1 (
    .Taste_Jahr(Eingangstaste_Jahr), .LED_3_7(Y_1_led_3_7), .LED_3_11(Y_1_led_3_11), .LED_4_7(Y_1_led_4_7),
    .LED_4_11(Y_1_led_4_11), .LED_5_8(Y_1_led_5_8), .LED_5_10(Y_1_led_5_10), .LED_6_9(Y_1_led_6_9),
    .LED_7_9(Y_1_led_7_9), .LED_8_9(Y_1_led_8_9));
  or or_1 (or_1_out, h_und_m_1_led_3_2, D_und_M_1_led_3_2);
  or or_2 (or_2_out, D_und_M_1_led_3_7, Y_1_led_3_7);
  or or_3 (or_3_out, D_und_M_1_led_3_11, Y_1_led_3_11);
  or or_4 (or_4_out, h_und_m_1_led_4_2, D_und_M_1_led_4_2);
  or or_5 (or_5_out, D_und_M_1_led_4_7, Y_1_led_4_7);
  or or_6 (or_6_out, m_und_s_1_led_4_8, D_und_M_1_led_4_8);
  or or_7 (or_7_out, m_und_s_1_led_4_10, D_und_M_1_led_4_10);
  or or_8 (or_8_out, D_und_M_1_led_4_11, Y_1_led_4_11);
  or or_9 (or_9_out, h_und_m_1_led_5_2, D_und_M_1_led_5_2, m_und_s_1_led_5_2);
  or or_10 (or_10_out, m_und_s_1_led_5_5, D_und_M_1_led_5_5);
  or or_11 (or_11_out, h_und_m_1_led_5_7, D_und_M_1_led_5_7);
  or or_12 (or_12_out, h_und_m_1_led_5_8, m_und_s_1_led_5_8, Y_1_led_5_8);
  or or_13 (or_13_out, h_und_m_1_led_5_9, D_und_M_1_led_5_9);
  or or_14 (or_14_out, h_und_m_1_led_5_10, Y_1_led_5_10);
  or or_15 (or_15_out, h_und_m_1_led_5_11, D_und_M_1_led_5_11);
  or or_16 (or_16_out, h_und_m_1_led_6_2, m_und_s_1_led_6_2, D_und_M_1_led_6_2);
  or or_17 (or_17_out, h_und_m_1_led_6_4, m_und_s_1_led_6_4);
  or or_18 (or_18_out, h_und_m_1_led_6_5, D_und_M_1_led_6_5);
  or or_19 (or_19_out, h_und_m_1_led_6_7, D_und_M_1_led_6_7);
  or or_20 (or_20_out, h_und_m_1_led_6_9, Y_1_led_6_9, m_und_s_1_led_6_9);
  or or_21 (or_21_out, h_und_m_1_led_6_11, D_und_M_1_led_6_11);
  or or_22 (or_22_out, h_und_m_1_led_7_2, m_und_s_1_led_7_2, D_und_M_1_led_7_2);
  or or_23 (or_23_out, m_und_s_1_led_7_4, D_und_M_1_led_7_4);
  or or_24 (or_24_out, D_und_M_1_led_7_7, h_und_m_1_led_7_7);
  or or_25 (or_25_out, h_und_m_1_led_7_9, Y_1_led_7_9);
  or or_26 (or_26_out, h_und_m_1_led_7_11, D_und_M_1_led_7_11);
  or or_27 (or_27_out, h_und_m_1_led_8_2, m_und_s_1_led_8_2, D_und_M_1_led_8_2);
  or or_28 (or_28_out, h_und_m_1_led_8_7, D_und_M_1_led_8_7);
  or or_29 (or_29_out, m_und_s_1_led_8_9, Y_1_led_8_9);
  or or_30 (or_30_out, h_und_m_1_led_8_11, D_und_M_1_led_8_11);
  xor xor_1 (LED_3_2, LED_Rahmen_Rest_Wecker, or_1_out);
  xor xor_2 (LED_3_3, LED_Rahmen_Rest_Wecker, D_und_M_1_led_3_3);
  xor xor_3 (LED_3_7, LED_Rahmen_Rest_Wecker, or_2_out);
  xor xor_4 (LED_3_11, LED_Rahmen_Rest_Wecker, or_3_out);
  xor xor_5 (LED_4_2, LED_Rahmen_Rest_Wecker, or_4_out);
  xor xor_6 (LED_4_4, LED_Rahmen_Rest_Wecker, D_und_M_1_led_4_4);
  xor xor_7 (LED_4_7, LED_Rahmen_Rest_Wecker, or_5_out);
  xor xor_8 (LED_4_8, LED_Rahmen_Rest_Wecker, or_6_out);
  xor xor_9 (LED_4_9, LED_Rahmen_Rest_Wecker, m_und_s_1_led_4_9);
  xor xor_10 (LED_4_10, LED_Rahmen_Rest_Wecker, or_7_out);
  xor xor_11 (LED_4_11, LED_Rahmen_Rest_Wecker, or_8_out);
  xor xor_12 (LED_5_2, LED_Rahmen_Rest_Wecker, or_9_out);
  xor xor_13 (LED_5_3, LED_Rahmen_Rest_Wecker, m_und_s_1_led_5_3);
  xor xor_14 (LED_5_4, LED_Rahmen_Rest_Wecker, m_und_s_1_led_5_4);
  xor xor_15 (LED_5_5, LED_Rahmen_Rest_Wecker, or_10_out);
  xor xor_16 (LED_5_6, LED_Rahmen_Rest_Wecker, m_und_s_1_led_5_6);
  xor xor_17 (LED_5_7, LED_Rahmen_Rest_Wecker, or_11_out);
  xor xor_18 (LED_5_8, LED_Rahmen_Rest_Wecker, or_12_out);
  xor xor_19 (LED_5_9, LED_Rahmen_Rest_Wecker, or_13_out);
  xor xor_20 (LED_5_10, LED_Rahmen_Rest_Wecker, or_14_out);
  xor xor_21 (LED_5_11, LED_Rahmen_Rest_Wecker, or_15_out);
  xor xor_22 (LED_6_2, LED_Rahmen_Rest_Wecker, or_16_out);
  xor xor_23 (LED_6_3, LED_Rahmen_Rest_Wecker, h_und_m_1_led_6_3);
  xor xor_24 (LED_6_4, LED_Rahmen_Rest_Wecker, or_17_out);
  xor xor_25 (LED_6_5, LED_Rahmen_Rest_Wecker, or_18_out);
  xor xor_26 (LED_6_6, LED_Rahmen_Rest_Wecker, m_und_s_1_led_6_6);
  xor xor_27 (LED_6_7, LED_Rahmen_Rest_Wecker, or_19_out);
  xor xor_28 (LED_6_8, LED_Rahmen_Rest_Wecker, m_und_s_1_led_6_8);
  xor xor_29 (LED_6_9, LED_Rahmen_Rest_Wecker, or_20_out);
  xor xor_30 (LED_6_10, LED_Rahmen_Rest_Wecker, m_und_s_1_led_6_10);
  xor xor_31 (LED_6_11, LED_Rahmen_Rest_Wecker, or_21_out);
  xor xor_32 (LED_7_2, LED_Rahmen_Rest_Wecker, or_22_out);
  xor xor_33 (LED_7_4, LED_Rahmen_Rest_Wecker, or_23_out);
  xor xor_34 (LED_7_5, LED_Rahmen_Rest_Wecker, h_und_m_1_led_7_5);
  xor xor_35 (LED_7_6, LED_Rahmen_Rest_Wecker, m_und_s_1_led_7_6);
  xor xor_36 (LED_7_7, LED_Rahmen_Rest_Wecker, or_24_out);
  xor xor_37 (LED_7_9, LED_Rahmen_Rest_Wecker, or_25_out);
  xor xor_38 (LED_7_10, LED_Rahmen_Rest_Wecker, m_und_s_1_led_7_10);
  xor xor_39 (LED_7_11, LED_Rahmen_Rest_Wecker, or_26_out);
  xor xor_40 (LED_8_2, LED_Rahmen_Rest_Wecker, or_27_out);
  xor xor_41 (LED_8_3, LED_Rahmen_Rest_Wecker, D_und_M_1_led_8_3);
  xor xor_42 (LED_8_5, LED_Rahmen_Rest_Wecker, h_und_m_1_led_8_5);
  xor xor_43 (LED_8_6, LED_Rahmen_Rest_Wecker, m_und_s_1_led_8_6);
  xor xor_44 (LED_8_7, LED_Rahmen_Rest_Wecker, or_28_out);
  xor xor_45 (LED_8_8, LED_Rahmen_Rest_Wecker, m_und_s_1_led_8_8);
  xor xor_46 (LED_8_9, LED_Rahmen_Rest_Wecker, or_29_out);
  xor xor_47 (LED_8_10, LED_Rahmen_Rest_Wecker, m_und_s_1_led_8_10);
  xor xor_48 (LED_8_11, LED_Rahmen_Rest_Wecker, or_30_out);
endmodule

module Part_Buntr1_Final (
);

  wire Hauptschaltung_LED_Anzeige_1_led_3_2, Hauptschaltung_LED_Anzeige_1_led_3_3,
       Hauptschaltung_LED_Anzeige_1_led_3_7, Hauptschaltung_LED_Anzeige_1_led_3_11,
       Hauptschaltung_LED_Anzeige_1_led_4_2, Hauptschaltung_LED_Anzeige_1_led_4_4,
       Hauptschaltung_LED_Anzeige_1_led_4_7, Hauptschaltung_LED_Anzeige_1_led_4_8,
       Hauptschaltung_LED_Anzeige_1_led_4_9, Hauptschaltung_LED_Anzeige_1_led_4_10,
       Hauptschaltung_LED_Anzeige_1_led_4_11, Hauptschaltung_LED_Anzeige_1_led_5_2,
       Hauptschaltung_LED_Anzeige_1_led_5_3, Hauptschaltung_LED_Anzeige_1_led_5_4,
       Hauptschaltung_LED_Anzeige_1_led_5_5, Hauptschaltung_LED_Anzeige_1_led_5_6,
       Hauptschaltung_LED_Anzeige_1_led_5_7, Hauptschaltung_LED_Anzeige_1_led_5_8,
       Hauptschaltung_LED_Anzeige_1_led_5_9, Hauptschaltung_LED_Anzeige_1_led_5_10,
       Hauptschaltung_LED_Anzeige_1_led_5_11, Hauptschaltung_LED_Anzeige_1_led_6_2,
       Hauptschaltung_LED_Anzeige_1_led_6_3, Hauptschaltung_LED_Anzeige_1_led_6_4,
       Hauptschaltung_LED_Anzeige_1_led_6_5, Hauptschaltung_LED_Anzeige_1_led_6_6,
       Hauptschaltung_LED_Anzeige_1_led_6_7, Hauptschaltung_LED_Anzeige_1_led_6_8,
       Hauptschaltung_LED_Anzeige_1_led_6_9, Hauptschaltung_LED_Anzeige_1_led_6_10,
       Hauptschaltung_LED_Anzeige_1_led_6_11, Hauptschaltung_LED_Anzeige_1_led_7_2,
       Hauptschaltung_LED_Anzeige_1_led_7_4, Hauptschaltung_LED_Anzeige_1_led_7_5,
       Hauptschaltung_LED_Anzeige_1_led_7_6, Hauptschaltung_LED_Anzeige_1_led_7_7,
       Hauptschaltung_LED_Anzeige_1_led_7_9, Hauptschaltung_LED_Anzeige_1_led_7_10,
       Hauptschaltung_LED_Anzeige_1_led_7_11, Hauptschaltung_LED_Anzeige_1_led_8_2,
       Hauptschaltung_LED_Anzeige_1_led_8_3, Hauptschaltung_LED_Anzeige_1_led_8_5,
       Hauptschaltung_LED_Anzeige_1_led_8_6, Hauptschaltung_LED_Anzeige_1_led_8_7,
       Hauptschaltung_LED_Anzeige_1_led_8_8, Hauptschaltung_LED_Anzeige_1_led_8_9,
       Hauptschaltung_LED_Anzeige_1_led_8_10, Hauptschaltung_LED_Anzeige_1_led_8_11,
       Hauptschaltung_LED_Anzeige_1_led_rahmen_rest_wecker, hpt_jahr_zu_led, hpt_min_sek_zu_led,
       hpt_reset_wecker_seg1, hpt_reset_wecker_seg2, hpt_reset_wecker_seg3_4, hpt_seg_1a, hpt_seg_1b,
       hpt_seg_1c, hpt_seg_1d, hpt_seg_1e, hpt_seg_1f, hpt_seg_1g, hpt_seg_2a, hpt_seg_2b, hpt_seg_2c,
       hpt_seg_2d, hpt_seg_2e, hpt_seg_2f, hpt_seg_2g, hpt_seg_3a, hpt_seg_3b, hpt_seg_3c, hpt_seg_3d,
       hpt_seg_3e, hpt_seg_3f, hpt_seg_3g, hpt_seg_4a, hpt_seg_4b, hpt_seg_4c, hpt_seg_4d, hpt_seg_4e,
       hpt_seg_4f, hpt_seg_4g, hpt_tag_mon_zu_led, hpt_weckerfunktion_zu_led, Schalter_wecker_sw1,
       Schalter_wecker_sw2, takt_down_takt_ausgang, Takt_out, Taste_gecko_1_out, Taste_gecko_2_out,
       Taste_gecko_3_out, Taste_gecko_4_out;
  wire [4:0] weckr_st_std_wecker_bit;
  wire [5:0] weckr_st_min_wecker_bits;

  DipSwitch #(.number(2)) Schalter_wecker (.sw1(Schalter_wecker_sw1), .sw2(Schalter_wecker_sw2));
  Clock Takt (.out(Takt_out));
  Button Taste_gecko_1 (.out(Taste_gecko_1_out));
  Button Taste_gecko_2 (.out(Taste_gecko_2_out));
  Button Taste_gecko_3 (.out(Taste_gecko_3_out));
  Button Taste_gecko_4 (.out(Taste_gecko_4_out));
  Wecker_stellen weckr_st (
    .Takt_2kHz(Takt_out), .Schalter_Gecko_Weckerstellen(Schalter_wecker_sw2),
    .Taster_Gecko_1(Taste_gecko_1_out), .Taster_Gecko_2(Taste_gecko_2_out),
    .Taster_Gecko_3(Taste_gecko_3_out), .Taster_Gecko_4(Taste_gecko_4_out),
    .Reset_seg1(hpt_reset_wecker_seg1), .Reset_seg2(hpt_reset_wecker_seg2),
    .Reset_seg3_4(hpt_reset_wecker_seg3_4), .Std_wecker_bit(weckr_st_std_wecker_bit),
    .min_wecker_bits(weckr_st_min_wecker_bits));
  kHz_4Hz takt_down (.Takt_Ausgang(takt_down_takt_ausgang), .Takt_Eingang(Takt_out));
  _7_Segment_Display L (
    .g(hpt_seg_1g), .f(hpt_seg_1f), .a(hpt_seg_1a), .b(hpt_seg_1b), .e(hpt_seg_1e), .d(hpt_seg_1d),
    .c(hpt_seg_1c));  // open: dp
  _7_Segment_Display LM (
    .g(hpt_seg_2g), .f(hpt_seg_2f), .a(hpt_seg_2a), .b(hpt_seg_2b), .e(hpt_seg_2e), .d(hpt_seg_2d),
    .c(hpt_seg_2c));  // open: dp
  _7_Segment_Display RM (
    .g(hpt_seg_3g), .f(hpt_seg_3f), .a(hpt_seg_3a), .b(hpt_seg_3b), .e(hpt_seg_3e), .d(hpt_seg_3d),
    .c(hpt_seg_3c));  // open: dp
  Hauptschaltung_7Seg_Anzeige hpt (
    .Seg_2A(hpt_seg_2a), .Seg_1D(hpt_seg_1d), .Seg_2C(hpt_seg_2c), .Seg_1G(hpt_seg_1g), .Seg_1C(hpt_seg_1c),
    .Takt_Wecker_Stellen(takt_down_takt_ausgang), .Taste_Gecko_Tag_Mon(Taste_gecko_2_out),
    .Schalter_Gecko_Wecker_Ein_Aus(Schalter_wecker_sw1), .Seg_2G(hpt_seg_2g), .Seg_2E(hpt_seg_2e),
    .Seg_2B(hpt_seg_2b), .Seg_2F(hpt_seg_2f), .Seg_2D(hpt_seg_2d), .Taste_Gecko_Jahr(Taste_gecko_3_out),
    .Schalter_Gecko_Wecker_Stellem(Schalter_wecker_sw2), .Seg_1A(hpt_seg_1a),
    .Taste_Gecko_Min_Sek(Taste_gecko_1_out), .Seg_1F(hpt_seg_1f), .Seg_1E(hpt_seg_1e), .Seg_1B(hpt_seg_1b),
    .Seg_3A(hpt_seg_3a), .Seg_3B(hpt_seg_3b), .Seg_3C(hpt_seg_3c), .Seg_3D(hpt_seg_3d), .Seg_3E(hpt_seg_3e),
    .Seg_3F(hpt_seg_3f), .Seg_3G(hpt_seg_3g), .Seg_4A(hpt_seg_4a), .Seg_4B(hpt_seg_4b), .Seg_4C(hpt_seg_4c),
    .Seg_4D(hpt_seg_4d), .Seg_4E(hpt_seg_4e), .Seg_4F(hpt_seg_4f), .Seg_4G(hpt_seg_4g),
    .Weckerfunktion_zu_LED(hpt_weckerfunktion_zu_led), .Min_sek_zu_LED(hpt_min_sek_zu_led),
    .Tag_Mon_zu_LED(hpt_tag_mon_zu_led), .Jahr_zu_LED(hpt_jahr_zu_led), .Stundenbits({5{1'b0}}),
    .Wecker_Stundenbits(weckr_st_std_wecker_bit), .Minutenbits({6{1'b0}}),
    .Wecker_Minutenbits(weckr_st_min_wecker_bits), .Sekundenbits({6{1'b0}}), .Jahrbits({7{1'b0}}),
    .Tagbits({5{1'b0}}), .Monatbits(4'b0000), .Reset_Wecker_Seg1(hpt_reset_wecker_seg1),
    .Reset_Wecker_Seg3_4(hpt_reset_wecker_seg3_4), .Reset_Wecker_Seg2(hpt_reset_wecker_seg2));
  _7_Segment_Display R (
    .g(hpt_seg_4g), .f(hpt_seg_4f), .a(hpt_seg_4a), .b(hpt_seg_4b), .e(hpt_seg_4e), .d(hpt_seg_4d),
    .c(hpt_seg_4c));  // open: dp
  LED LED_2 (.in(Hauptschaltung_LED_Anzeige_1_led_rahmen_rest_wecker));
  LED LED_1 (.in(Hauptschaltung_LED_Anzeige_1_led_rahmen_rest_wecker));
  LED LED_13 (.in(Hauptschaltung_LED_Anzeige_1_led_rahmen_rest_wecker));
  LED LED_14 (.in(Hauptschaltung_LED_Anzeige_1_led_rahmen_rest_wecker));
  LED LED_25 (.in(Hauptschaltung_LED_Anzeige_1_led_rahmen_rest_wecker));
  LED LED_26 (.in(Hauptschaltung_LED_Anzeige_1_led_3_2));
  LED LED_37 (.in(Hauptschaltung_LED_Anzeige_1_led_rahmen_rest_wecker));
  LED LED_38 (.in(Hauptschaltung_LED_Anzeige_1_led_4_2));
  LED LED_49 (.in(Hauptschaltung_LED_Anzeige_1_led_rahmen_rest_wecker));
  LED LED_50 (.in(Hauptschaltung_LED_Anzeige_1_led_5_2));
  LED LED_61 (.in(Hauptschaltung_LED_Anzeige_1_led_rahmen_rest_wecker));
  LED LED_62 (.in(Hauptschaltung_LED_Anzeige_1_led_6_2));
  LED LED_73 (.in(Hauptschaltung_LED_Anzeige_1_led_rahmen_rest_wecker));
  LED LED_74 (.in(Hauptschaltung_LED_Anzeige_1_led_7_2));
  LED LED_86 (.in(Hauptschaltung_LED_Anzeige_1_led_8_2));
  LED LED_85 (.in(Hauptschaltung_LED_Anzeige_1_led_rahmen_rest_wecker));
  LED LED_97 (.in(Hauptschaltung_LED_Anzeige_1_led_rahmen_rest_wecker));
  LED LED_98 (.in(Hauptschaltung_LED_Anzeige_1_led_rahmen_rest_wecker));
  LED LED_110 (.in(Hauptschaltung_LED_Anzeige_1_led_rahmen_rest_wecker));
  LED LED_109 (.in(Hauptschaltung_LED_Anzeige_1_led_rahmen_rest_wecker));
  LED LED_4 (.in(Hauptschaltung_LED_Anzeige_1_led_rahmen_rest_wecker));
  LED LED_3 (.in(Hauptschaltung_LED_Anzeige_1_led_rahmen_rest_wecker));
  LED LED_16 (.in(Hauptschaltung_LED_Anzeige_1_led_rahmen_rest_wecker));
  LED LED_15 (.in(Hauptschaltung_LED_Anzeige_1_led_rahmen_rest_wecker));
  LED LED_27 (.in(Hauptschaltung_LED_Anzeige_1_led_3_3));
  LED LED_28 (.in(Hauptschaltung_LED_Anzeige_1_led_rahmen_rest_wecker));
  LED LED_40 (.in(Hauptschaltung_LED_Anzeige_1_led_4_4));
  LED LED_39 (.in(Hauptschaltung_LED_Anzeige_1_led_rahmen_rest_wecker));
  LED LED_52 (.in(Hauptschaltung_LED_Anzeige_1_led_5_4));
  LED LED_51 (.in(Hauptschaltung_LED_Anzeige_1_led_5_3));
  LED LED_64 (.in(Hauptschaltung_LED_Anzeige_1_led_6_4));
  LED LED_63 (.in(Hauptschaltung_LED_Anzeige_1_led_6_3));
  LED LED_75 (.in(Hauptschaltung_LED_Anzeige_1_led_rahmen_rest_wecker));
  LED LED_76 (.in(Hauptschaltung_LED_Anzeige_1_led_7_4));
  LED LED_88 (.in(Hauptschaltung_LED_Anzeige_1_led_rahmen_rest_wecker));
  LED LED_87 (.in(Hauptschaltung_LED_Anzeige_1_led_8_3));
  LED LED_100 (.in(Hauptschaltung_LED_Anzeige_1_led_rahmen_rest_wecker));
  LED LED_99 (.in(Hauptschaltung_LED_Anzeige_1_led_rahmen_rest_wecker));
  LED LED_111 (.in(Hauptschaltung_LED_Anzeige_1_led_rahmen_rest_wecker));
  LED LED_112 (.in(Hauptschaltung_LED_Anzeige_1_led_rahmen_rest_wecker));
  LED LED_6 (.in(Hauptschaltung_LED_Anzeige_1_led_rahmen_rest_wecker));
  LED LED_5 (.in(Hauptschaltung_LED_Anzeige_1_led_rahmen_rest_wecker));
  LED LED_17 (.in(Hauptschaltung_LED_Anzeige_1_led_rahmen_rest_wecker));
  LED LED_18 (.in(Hauptschaltung_LED_Anzeige_1_led_rahmen_rest_wecker));
  LED LED_30 (.in(Hauptschaltung_LED_Anzeige_1_led_rahmen_rest_wecker));
  LED LED_29 (.in(Hauptschaltung_LED_Anzeige_1_led_rahmen_rest_wecker));
  LED LED_41 (.in(Hauptschaltung_LED_Anzeige_1_led_rahmen_rest_wecker));
  LED LED_42 (.in(Hauptschaltung_LED_Anzeige_1_led_rahmen_rest_wecker));
  LED LED_53 (.in(Hauptschaltung_LED_Anzeige_1_led_5_5));
  LED LED_54 (.in(Hauptschaltung_LED_Anzeige_1_led_5_6));
  LED LED_65 (.in(Hauptschaltung_LED_Anzeige_1_led_6_5));
  LED LED_66 (.in(Hauptschaltung_LED_Anzeige_1_led_6_6));
  LED LED_78 (.in(Hauptschaltung_LED_Anzeige_1_led_7_6));
  LED LED_77 (.in(Hauptschaltung_LED_Anzeige_1_led_7_5));
  LED LED_89 (.in(Hauptschaltung_LED_Anzeige_1_led_8_5));
  LED LED_90 (.in(Hauptschaltung_LED_Anzeige_1_led_8_6));
  LED LED_101 (.in(Hauptschaltung_LED_Anzeige_1_led_rahmen_rest_wecker));
  LED LED_102 (.in(Hauptschaltung_LED_Anzeige_1_led_rahmen_rest_wecker));
  LED LED_113 (.in(Hauptschaltung_LED_Anzeige_1_led_rahmen_rest_wecker));
  LED LED_114 (.in(Hauptschaltung_LED_Anzeige_1_led_rahmen_rest_wecker));
  LED LED_7 (.in(Hauptschaltung_LED_Anzeige_1_led_rahmen_rest_wecker));
  LED LED_8 (.in(Hauptschaltung_LED_Anzeige_1_led_rahmen_rest_wecker));
  LED LED_19 (.in(Hauptschaltung_LED_Anzeige_1_led_rahmen_rest_wecker));
  LED LED_20 (.in(Hauptschaltung_LED_Anzeige_1_led_rahmen_rest_wecker));
  LED LED_32 (.in(Hauptschaltung_LED_Anzeige_1_led_rahmen_rest_wecker));
  LED LED_31 (.in(Hauptschaltung_LED_Anzeige_1_led_3_7));
  LED LED_44 (.in(Hauptschaltung_LED_Anzeige_1_led_4_8));
  LED LED_43 (.in(Hauptschaltung_LED_Anzeige_1_led_4_7));
  LED LED_56 (.in(Hauptschaltung_LED_Anzeige_1_led_5_8));
  LED LED_55 (.in(Hauptschaltung_LED_Anzeige_1_led_5_7));
  LED LED_67 (.in(Hauptschaltung_LED_Anzeige_1_led_6_7));
  LED LED_68 (.in(Hauptschaltung_LED_Anzeige_1_led_6_8));
  LED LED_79 (.in(Hauptschaltung_LED_Anzeige_1_led_7_7));
  LED LED_80 (.in(Hauptschaltung_LED_Anzeige_1_led_rahmen_rest_wecker));
  LED LED_92 (.in(Hauptschaltung_LED_Anzeige_1_led_8_8));
  LED LED_91 (.in(Hauptschaltung_LED_Anzeige_1_led_8_7));
  LED LED_103 (.in(Hauptschaltung_LED_Anzeige_1_led_rahmen_rest_wecker));
  LED LED_104 (.in(Hauptschaltung_LED_Anzeige_1_led_rahmen_rest_wecker));
  LED LED_116 (.in(Hauptschaltung_LED_Anzeige_1_led_rahmen_rest_wecker));
  LED LED_115 (.in(Hauptschaltung_LED_Anzeige_1_led_rahmen_rest_wecker));
  LED LED_9 (.in(Hauptschaltung_LED_Anzeige_1_led_rahmen_rest_wecker));
  LED LED_10 (.in(Hauptschaltung_LED_Anzeige_1_led_rahmen_rest_wecker));
  LED LED_22 (.in(Hauptschaltung_LED_Anzeige_1_led_rahmen_rest_wecker));
  LED LED_21 (.in(Hauptschaltung_LED_Anzeige_1_led_rahmen_rest_wecker));
  LED LED_33 (.in(Hauptschaltung_LED_Anzeige_1_led_rahmen_rest_wecker));
  LED LED_34 (.in(Hauptschaltung_LED_Anzeige_1_led_rahmen_rest_wecker));
  LED LED_45 (.in(Hauptschaltung_LED_Anzeige_1_led_4_9));
  LED LED_46 (.in(Hauptschaltung_LED_Anzeige_1_led_4_10));
  LED LED_58 (.in(Hauptschaltung_LED_Anzeige_1_led_5_10));
  LED LED_57 (.in(Hauptschaltung_LED_Anzeige_1_led_5_9));
  LED LED_69 (.in(Hauptschaltung_LED_Anzeige_1_led_6_9));
  LED LED_70 (.in(Hauptschaltung_LED_Anzeige_1_led_6_10));
  LED LED_81 (.in(Hauptschaltung_LED_Anzeige_1_led_7_9));
  LED LED_82 (.in(Hauptschaltung_LED_Anzeige_1_led_7_10));
  LED LED_94 (.in(Hauptschaltung_LED_Anzeige_1_led_8_10));
  LED LED_93 (.in(Hauptschaltung_LED_Anzeige_1_led_8_9));
  LED LED_105 (.in(Hauptschaltung_LED_Anzeige_1_led_rahmen_rest_wecker));
  LED LED_106 (.in(Hauptschaltung_LED_Anzeige_1_led_rahmen_rest_wecker));
  LED LED_118 (.in(Hauptschaltung_LED_Anzeige_1_led_rahmen_rest_wecker));
  LED LED_117 (.in(Hauptschaltung_LED_Anzeige_1_led_rahmen_rest_wecker));
  LED LED_11 (.in(Hauptschaltung_LED_Anzeige_1_led_rahmen_rest_wecker));
  LED LED_12 (.in(Hauptschaltung_LED_Anzeige_1_led_rahmen_rest_wecker));
  LED LED_23 (.in(Hauptschaltung_LED_Anzeige_1_led_rahmen_rest_wecker));
  LED LED_24 (.in(Hauptschaltung_LED_Anzeige_1_led_rahmen_rest_wecker));
  LED LED_35 (.in(Hauptschaltung_LED_Anzeige_1_led_3_11));
  LED LED_36 (.in(Hauptschaltung_LED_Anzeige_1_led_rahmen_rest_wecker));
  LED LED_48 (.in(Hauptschaltung_LED_Anzeige_1_led_rahmen_rest_wecker));
  LED LED_47 (.in(Hauptschaltung_LED_Anzeige_1_led_4_11));
  LED LED_60 (.in(Hauptschaltung_LED_Anzeige_1_led_rahmen_rest_wecker));
  LED LED_59 (.in(Hauptschaltung_LED_Anzeige_1_led_5_11));
  LED LED_71 (.in(Hauptschaltung_LED_Anzeige_1_led_6_11));
  LED LED_72 (.in(Hauptschaltung_LED_Anzeige_1_led_rahmen_rest_wecker));
  LED LED_83 (.in(Hauptschaltung_LED_Anzeige_1_led_7_11));
  LED LED_84 (.in(Hauptschaltung_LED_Anzeige_1_led_rahmen_rest_wecker));
  LED LED_96 (.in(Hauptschaltung_LED_Anzeige_1_led_rahmen_rest_wecker));
  LED LED_95 (.in(Hauptschaltung_LED_Anzeige_1_led_8_11));
  LED LED_107 (.in(Hauptschaltung_LED_Anzeige_1_led_rahmen_rest_wecker));
  LED LED_108 (.in(Hauptschaltung_LED_Anzeige_1_led_rahmen_rest_wecker));
  LED LED_119 (.in(Hauptschaltung_LED_Anzeige_1_led_rahmen_rest_wecker));
  LED LED_120 (.in(Hauptschaltung_LED_Anzeige_1_led_rahmen_rest_wecker));
  Hauptschaltung_LED_Anzeige Hauptschaltung_LED_Anzeige_1 (
    .LED_6_10(Hauptschaltung_LED_Anzeige_1_led_6_10), .LED_6_8(Hauptschaltung_LED_Anzeige_1_led_6_8),
    .LED_6_9(Hauptschaltung_LED_Anzeige_1_led_6_9), .LED_6_11(Hauptschaltung_LED_Anzeige_1_led_6_11),
    .LED_6_7(Hauptschaltung_LED_Anzeige_1_led_6_7), .LED_6_6(Hauptschaltung_LED_Anzeige_1_led_6_6),
    .LED_6_5(Hauptschaltung_LED_Anzeige_1_led_6_5), .LED_6_4(Hauptschaltung_LED_Anzeige_1_led_6_4),
    .LED_6_3(Hauptschaltung_LED_Anzeige_1_led_6_3), .LED_6_2(Hauptschaltung_LED_Anzeige_1_led_6_2),
    .LED_5_11(Hauptschaltung_LED_Anzeige_1_led_5_11), .LED_5_10(Hauptschaltung_LED_Anzeige_1_led_5_10),
    .LED_5_9(Hauptschaltung_LED_Anzeige_1_led_5_9), .LED_5_8(Hauptschaltung_LED_Anzeige_1_led_5_8),
    .LED_5_7(Hauptschaltung_LED_Anzeige_1_led_5_7), .LED_5_6(Hauptschaltung_LED_Anzeige_1_led_5_6),
    .LED_5_5(Hauptschaltung_LED_Anzeige_1_led_5_5), .LED_5_4(Hauptschaltung_LED_Anzeige_1_led_5_4),
    .LED_5_3(Hauptschaltung_LED_Anzeige_1_led_5_3), .LED_5_2(Hauptschaltung_LED_Anzeige_1_led_5_2),
    .LED_4_11(Hauptschaltung_LED_Anzeige_1_led_4_11), .LED_4_10(Hauptschaltung_LED_Anzeige_1_led_4_10),
    .LED_4_9(Hauptschaltung_LED_Anzeige_1_led_4_9), .LED_4_8(Hauptschaltung_LED_Anzeige_1_led_4_8),
    .LED_4_7(Hauptschaltung_LED_Anzeige_1_led_4_7), .LED_4_4(Hauptschaltung_LED_Anzeige_1_led_4_4),
    .LED_4_2(Hauptschaltung_LED_Anzeige_1_led_4_2), .LED_3_11(Hauptschaltung_LED_Anzeige_1_led_3_11),
    .LED_3_7(Hauptschaltung_LED_Anzeige_1_led_3_7), .LED_3_3(Hauptschaltung_LED_Anzeige_1_led_3_3),
    .LED_3_2(Hauptschaltung_LED_Anzeige_1_led_3_2),
    .LED_Rahmen_Rest_Wecker(Hauptschaltung_LED_Anzeige_1_led_rahmen_rest_wecker),
    .Eingangstaste_Jahr(hpt_jahr_zu_led), .Eingangstaste_Tag_Monat(hpt_tag_mon_zu_led),
    .Eingangstaste_Min_Sek(hpt_min_sek_zu_led), .Weckfunktion(hpt_weckerfunktion_zu_led),
    .Input_1(takt_down_takt_ausgang), .LED_7_2(Hauptschaltung_LED_Anzeige_1_led_7_2),
    .LED_7_4(Hauptschaltung_LED_Anzeige_1_led_7_4), .LED_7_5(Hauptschaltung_LED_Anzeige_1_led_7_5),
    .LED_7_6(Hauptschaltung_LED_Anzeige_1_led_7_6), .LED_7_7(Hauptschaltung_LED_Anzeige_1_led_7_7),
    .LED_7_9(Hauptschaltung_LED_Anzeige_1_led_7_9), .LED_7_10(Hauptschaltung_LED_Anzeige_1_led_7_10),
    .LED_7_11(Hauptschaltung_LED_Anzeige_1_led_7_11), .LED_8_2(Hauptschaltung_LED_Anzeige_1_led_8_2),
    .LED_8_3(Hauptschaltung_LED_Anzeige_1_led_8_3), .LED_8_5(Hauptschaltung_LED_Anzeige_1_led_8_5),
    .LED_8_6(Hauptschaltung_LED_Anzeige_1_led_8_6), .LED_8_7(Hauptschaltung_LED_Anzeige_1_led_8_7),
    .LED_8_8(Hauptschaltung_LED_Anzeige_1_led_8_8), .LED_8_9(Hauptschaltung_LED_Anzeige_1_led_8_9),
    .LED_8_10(Hauptschaltung_LED_Anzeige_1_led_8_10), .LED_8_11(Hauptschaltung_LED_Anzeige_1_led_8_11));
endmodule

module h_und_m (
  input  Taste_min_sek,
  input  Taste_tag_mon,
  input  Taste_jahr,
  output LED_3_2,
  output LED_4_2,
  output LED_5_2,
  output LED_5_7,
  output LED_5_8,
  output LED_5_9,
  output LED_5_10,
  output LED_5_11,
  output LED_6_2,
  output LED_6_3,
  output LED_6_4,
  output LED_6_5,
  output LED_6_7,
  output LED_6_9,
  output LED_6_11,
  output LED_7_2,
  output LED_7_5,
  output LED_7_7,
  output LED_7_9,
  output LED_7_11,
  output LED_8_2,
  output LED_8_5,
  output LED_8_7,
  output LED_8_11
);

  and and_1 (LED_3_2, ~Taste_min_sek, ~Taste_tag_mon, ~Taste_jahr);  // AND_Gate

  assign LED_4_2 = LED_3_2;
  assign LED_5_2 = LED_3_2;
  assign LED_5_7 = LED_3_2;
  assign LED_5_8 = LED_3_2;
  assign LED_5_9 = LED_3_2;
  assign LED_5_10 = LED_3_2;
  assign LED_5_11 = LED_3_2;
  assign LED_6_2 = LED_3_2;
  assign LED_6_3 = LED_3_2;
  assign LED_6_4 = LED_3_2;
  assign LED_6_5 = LED_3_2;
  assign LED_6_7 = LED_3_2;
  assign LED_6_9 = LED_3_2;
  assign LED_6_11 = LED_3_2;
  assign LED_7_2 = LED_3_2;
  assign LED_7_5 = LED_3_2;
  assign LED_7_7 = LED_3_2;
  assign LED_7_9 = LED_3_2;
  assign LED_7_11 = LED_3_2;
  assign LED_8_2 = LED_3_2;
  assign LED_8_5 = LED_3_2;
  assign LED_8_7 = LED_3_2;
  assign LED_8_11 = LED_3_2;
endmodule

module m_und_s (
  input  Taste_min_sek,
  output LED_4_8,
  output LED_4_9,
  output LED_4_10,
  output LED_5_2,
  output LED_5_3,
  output LED_5_4,
  output LED_5_5,
  output LED_5_6,
  output LED_5_8,
  output LED_6_2,
  output LED_6_4,
  output LED_6_6,
  output LED_6_8,
  output LED_6_9,
  output LED_6_10,
  output LED_7_2,
  output LED_7_4,
  output LED_7_6,
  output LED_7_10,
  output LED_8_2,
  output LED_8_6,
  output LED_8_8,
  output LED_8_9,
  output LED_8_10
);


  assign LED_4_8 = Taste_min_sek;
  assign LED_4_9 = Taste_min_sek;
  assign LED_4_10 = Taste_min_sek;
  assign LED_5_2 = Taste_min_sek;
  assign LED_5_3 = Taste_min_sek;
  assign LED_5_4 = Taste_min_sek;
  assign LED_5_5 = Taste_min_sek;
  assign LED_5_6 = Taste_min_sek;
  assign LED_5_8 = Taste_min_sek;
  assign LED_6_2 = Taste_min_sek;
  assign LED_6_4 = Taste_min_sek;
  assign LED_6_6 = Taste_min_sek;
  assign LED_6_8 = Taste_min_sek;
  assign LED_6_9 = Taste_min_sek;
  assign LED_6_10 = Taste_min_sek;
  assign LED_7_2 = Taste_min_sek;
  assign LED_7_4 = Taste_min_sek;
  assign LED_7_6 = Taste_min_sek;
  assign LED_7_10 = Taste_min_sek;
  assign LED_8_2 = Taste_min_sek;
  assign LED_8_6 = Taste_min_sek;
  assign LED_8_8 = Taste_min_sek;
  assign LED_8_9 = Taste_min_sek;
  assign LED_8_10 = Taste_min_sek;
endmodule

module D_und_M (
  input  Taste_Tag_Monat,
  output LED_3_2,
  output LED_3_3,
  output LED_3_7,
  output LED_3_11,
  output LED_4_2,
  output LED_4_4,
  output LED_4_7,
  output LED_4_8,
  output LED_4_10,
  output LED_4_11,
  output LED_5_2,
  output LED_5_5,
  output LED_5_7,
  output LED_5_9,
  output LED_5_11,
  output LED_6_2,
  output LED_6_5,
  output LED_6_7,
  output LED_6_11,
  output LED_7_2,
  output LED_7_4,
  output LED_7_7,
  output LED_7_11,
  output LED_8_2,
  output LED_8_3,
  output LED_8_7,
  output LED_8_11
);


  assign LED_3_2 = Taste_Tag_Monat;
  assign LED_3_3 = Taste_Tag_Monat;
  assign LED_3_7 = Taste_Tag_Monat;
  assign LED_3_11 = Taste_Tag_Monat;
  assign LED_4_2 = Taste_Tag_Monat;
  assign LED_4_4 = Taste_Tag_Monat;
  assign LED_4_7 = Taste_Tag_Monat;
  assign LED_4_8 = Taste_Tag_Monat;
  assign LED_4_10 = Taste_Tag_Monat;
  assign LED_4_11 = Taste_Tag_Monat;
  assign LED_5_2 = Taste_Tag_Monat;
  assign LED_5_5 = Taste_Tag_Monat;
  assign LED_5_7 = Taste_Tag_Monat;
  assign LED_5_9 = Taste_Tag_Monat;
  assign LED_5_11 = Taste_Tag_Monat;
  assign LED_6_2 = Taste_Tag_Monat;
  assign LED_6_5 = Taste_Tag_Monat;
  assign LED_6_7 = Taste_Tag_Monat;
  assign LED_6_11 = Taste_Tag_Monat;
  assign LED_7_2 = Taste_Tag_Monat;
  assign LED_7_4 = Taste_Tag_Monat;
  assign LED_7_7 = Taste_Tag_Monat;
  assign LED_7_11 = Taste_Tag_Monat;
  assign LED_8_2 = Taste_Tag_Monat;
  assign LED_8_3 = Taste_Tag_Monat;
  assign LED_8_7 = Taste_Tag_Monat;
  assign LED_8_11 = Taste_Tag_Monat;
endmodule

module Y (
  input  Taste_Jahr,
  output LED_3_7,
  output LED_3_11,
  output LED_4_7,
  output LED_4_11,
  output LED_5_8,
  output LED_5_10,
  output LED_6_9,
  output LED_7_9,
  output LED_8_9
);


  assign LED_3_7 = Taste_Jahr;
  assign LED_3_11 = Taste_Jahr;
  assign LED_4_7 = Taste_Jahr;
  assign LED_4_11 = Taste_Jahr;
  assign LED_5_8 = Taste_Jahr;
  assign LED_5_10 = Taste_Jahr;
  assign LED_6_9 = Taste_Jahr;
  assign LED_7_9 = Taste_Jahr;
  assign LED_8_9 = Taste_Jahr;
endmodule

module kHz_4Hz (
  input  Takt_Eingang,
  output Takt_Ausgang
);

  wire countr9bit_p2, d_ff_1_qn;
  wire [8:0] countr9bit_p5;

  // Counter_9bit countr9bit: pin names not known; wires that end beside it: Takt_Eingang, countr9bit_p2, 1'b0, {9{1'b0}}, countr9bit_p5
  D_Flip_Flop d_ff_1 (.D(d_ff_1_qn), .clk(countr9bit_p2), .Q(Takt_Ausgang), .Qn(d_ff_1_qn));  // open: preset, reset
  and and_1 (countr9bit_p2, countr9bit_p5[0], countr9bit_p5[1], countr9bit_p5[2], countr9bit_p5[3], countr9bit_p5[4], countr9bit_p5[5], countr9bit_p5[6], countr9bit_p5[7], countr9bit_p5[8]);
endmodule

module Wecker_stellen (
  input  Takt_2kHz,
  input  Schalter_Gecko_Weckerstellen,
  input  Taster_Gecko_1,
  input  Taster_Gecko_2,
  input  Taster_Gecko_3,
  input  Taster_Gecko_4,
  input  Reset_seg1,
  input  Reset_seg2,
  input  Reset_seg3_4,
  output [4:0] Std_wecker_bit,
  output [5:0] min_wecker_bits
);

  wire and_1_out, and_2_out, and_3_out, and_4_out, and_5_out, and_6_out, and_7_out, and_8_out, and_9_out,
       and_10_out, or_1_out, or_2_out, or_3_out, or_4_out, or_5_out, or_6_out, tkt_w_st1_takt_weckerstellen,
       tkt_w_st3_takt_weckerstellen, tkt_w_st_2_takt_weckerstellen, tkt_w_st_takt_weckerstellen;
  wire [8:0] ctr9bit1_positiv, ctr9bit2_positiv, ctr9bit3_positiv, ctr9bit_positiv;

  and and_1 (and_1_out, Schalter_Gecko_Weckerstellen, Taster_Gecko_1);
  and and_2 (and_2_out, Schalter_Gecko_Weckerstellen, Taster_Gecko_2);
  and and_3 (and_3_out, Schalter_Gecko_Weckerstellen, Taster_Gecko_3);
  and and_4 (and_4_out, Schalter_Gecko_Weckerstellen, Taster_Gecko_4);
  kHz_2Hz tkt_w_st (.Takt_Weckerstellen(tkt_w_st_takt_weckerstellen), .Takt_2kHz(Takt_2kHz), .Taste(and_1_out));
  kHz_2Hz tkt_w_st1 (.Takt_Weckerstellen(tkt_w_st1_takt_weckerstellen), .Takt_2kHz(Takt_2kHz), .Taste(and_2_out));
  kHz_2Hz tkt_w_st_2 (.Takt_Weckerstellen(tkt_w_st_2_takt_weckerstellen), .Takt_2kHz(Takt_2kHz), .Taste(and_3_out));
  kHz_2Hz tkt_w_st3 (.Takt_Weckerstellen(tkt_w_st3_takt_weckerstellen), .Takt_2kHz(Takt_2kHz), .Taste(and_4_out));
  or or_1 (or_1_out, Reset_seg1, Reset_seg2);
  or or_2 (or_2_out, ctr9bit1_positiv[3], ctr9bit1_positiv[2]);
  and and_5 (and_5_out, ctr9bit_positiv[3], ctr9bit_positiv[1], or_2_out);
  and and_6 (and_6_out, and_9_out, ctr9bit1_positiv[0], ctr9bit1_positiv[1]);
  or or_3 (or_3_out, and_7_out, Reset_seg3_4);
  or or_4 (or_4_out, Reset_seg3_4, and_8_out);
  or or_5 (or_5_out, and_9_out, and_5_out, or_1_out);
  or or_6 (or_6_out, and_6_out, or_1_out, and_10_out);
  Counter9Bit ctr9bit2 (
    .clock(tkt_w_st_2_takt_weckerstellen), .reset(or_3_out), .fix0(1'b0), .bits_to_add10(Taster_Gecko_3),
    .bits_to_add1(1'b0), .positiv(ctr9bit2_positiv));  // open: negiert
  Counter9Bit ctr9bit3 (
    .clock(tkt_w_st3_takt_weckerstellen), .reset(or_4_out), .fix0(1'b0), .bits_to_add10(1'b0),
    .bits_to_add1(Taster_Gecko_4), .positiv(ctr9bit3_positiv));  // open: negiert
  Counter9Bit ctr9bit (
    .clock(tkt_w_st_takt_weckerstellen), .reset(or_5_out), .fix0(1'b0), .bits_to_add10(Taster_Gecko_1),
    .bits_to_add1(1'b0), .positiv(ctr9bit_positiv));  // open: negiert
  Counter9Bit ctr9bit1 (
    .clock(tkt_w_st1_takt_weckerstellen), .reset(or_6_out), .fix0(1'b0), .bits_to_add10(1'b0),
    .bits_to_add1(Taster_Gecko_2), .positiv(ctr9bit1_positiv));  // open: negiert
  and and_7 (and_7_out, ~ctr9bit2_positiv[0], ctr9bit2_positiv[1], ~ctr9bit2_positiv[2], ~ctr9bit2_positiv[3], ctr9bit2_positiv[4], ctr9bit2_positiv[5], ~ctr9bit2_positiv[6], ~ctr9bit2_positiv[7], ~ctr9bit2_positiv[8]);  // AND_Gate
  and and_8 (and_8_out, ctr9bit3_positiv[0], ~ctr9bit3_positiv[1], ~ctr9bit3_positiv[2], ctr9bit3_positiv[3], ~ctr9bit3_positiv[4], ~ctr9bit3_positiv[5], ~ctr9bit3_positiv[6], ~ctr9bit3_positiv[7], ~ctr9bit3_positiv[8]);  // AND_Gate
  and and_9 (and_9_out, ~ctr9bit_positiv[0], ~ctr9bit_positiv[1], ctr9bit_positiv[2], ~ctr9bit_positiv[3], ctr9bit_positiv[4], ~ctr9bit_positiv[5], ~ctr9bit_positiv[6], ~ctr9bit_positiv[7], ~ctr9bit_positiv[8]);  // AND_Gate
  add6bit adder6bit (
    .Minus(1'b0), .C_IN(1'b0), .A0(ctr9bit2_positiv[0]), .A1(ctr9bit2_positiv[1]), .A2(ctr9bit2_positiv[2]),
    .A3(ctr9bit2_positiv[3]), .A4(ctr9bit2_positiv[4]), .A5(ctr9bit2_positiv[5]), .B0(ctr9bit3_positiv[0]),
    .B1(ctr9bit3_positiv[1]), .B2(ctr9bit3_positiv[2]), .B3(ctr9bit3_positiv[3]), .B4(ctr9bit3_positiv[4]),
    .B5(ctr9bit3_positiv[5]), .S0(min_wecker_bits[0]), .S1(min_wecker_bits[1]), .S2(min_wecker_bits[2]),
    .S3(min_wecker_bits[3]), .S4(min_wecker_bits[4]), .S5(min_wecker_bits[5]));  // open: C_OUT
  add5bit adder5bit (
    .Minus(1'b0), .C_IN(1'b0), .A0(ctr9bit_positiv[0]), .A1(ctr9bit_positiv[1]), .A2(ctr9bit_positiv[2]),
    .A3(ctr9bit_positiv[3]), .A4(ctr9bit_positiv[4]), .B0(ctr9bit1_positiv[0]), .B1(ctr9bit1_positiv[1]),
    .B2(ctr9bit1_positiv[2]), .B3(ctr9bit1_positiv[3]), .B4(ctr9bit1_positiv[4]), .S0(Std_wecker_bit[0]),
    .S1(Std_wecker_bit[1]), .S2(Std_wecker_bit[2]), .S3(Std_wecker_bit[3]), .S4(Std_wecker_bit[4]));  // open: C_OUT
  and and_10 (and_10_out, ctr9bit1_positiv[0], ~ctr9bit1_positiv[1], ~ctr9bit1_positiv[2], ctr9bit1_positiv[3], ~ctr9bit1_positiv[4], ~ctr9bit1_positiv[5], ~ctr9bit1_positiv[6], ~ctr9bit1_positiv[7], ~ctr9bit1_positiv[8]);  // AND_Gate
endmodule

module kHz_2Hz (
  input  Takt_2kHz,
  input  Taste,
  output Takt_Weckerstellen
);

  wire and_1_out, and_2_out, d_ff_1_qn, or_1_out;
  wire [12:0] countr1bit_p5;

  and and_1 (and_1_out, Takt_2kHz, Taste);
  or or_1 (or_1_out, ~Taste, and_2_out);  // OR_Gate
  // Counter_13bit countr1bit: pin names not known; wires that end beside it: and_1_out, or_1_out, 1'b0, {13{1'b0}}, countr1bit_p5
  and and_2 (and_2_out, ~countr1bit_p5[0], ~countr1bit_p5[1], ~countr1bit_p5[2], countr1bit_p5[3], ~countr1bit_p5[4], countr1bit_p5[5], countr1bit_p5[6], countr1bit_p5[7], countr1bit_p5[8], countr1bit_p5[9], ~countr1bit_p5[10], ~countr1bit_p5[11], ~countr1bit_p5[12]);  // AND_Gate
  D_Flip_Flop d_ff_1 (.D(d_ff_1_qn), .clk(and_2_out), .Q(Takt_Weckerstellen), .Qn(d_ff_1_qn));  // open: preset, reset
endmodule

module Counter9Bit (
  input  clock,
  input  reset,
  input  fix0,
  input  bits_to_add10,
  input  bits_to_add1,
  output [8:0] positiv,
  output [8:0] negiert
);

  wire addr_p5;
  wire [8:0] multiplx9bit_p5;

  // add9bit addr: pin names not known; wires that end beside it: 1'b0, 1'b0, positiv, {{5{1'b0}}, bits_to_add10, 1'b0, bits_to_add10, bits_to_add1}, addr_p5
  // Multiplexer_9bit multiplx9bit: pin names not known; wires that end beside it: {fix0, reset}, addr_p5, {9{1'b0}}, {9{1'b0}}, multiplx9bit_p5
  D_Flip_Flop d_ff_1 (.D(multiplx9bit_p5[0]), .clk(clock), .Q(positiv[0]), .Qn(negiert[0]));  // open: preset, reset
  D_Flip_Flop d_ff_2 (.D(multiplx9bit_p5[1]), .clk(clock), .Q(positiv[1]), .Qn(negiert[1]));  // open: preset, reset
  D_Flip_Flop d_ff_3 (.D(multiplx9bit_p5[2]), .clk(clock), .Q(positiv[2]), .Qn(negiert[2]));  // open: preset, reset
  D_Flip_Flop d_ff_4 (.D(multiplx9bit_p5[3]), .clk(clock), .Q(positiv[3]), .Qn(negiert[3]));  // open: preset, reset
  D_Flip_Flop d_ff_5 (.D(multiplx9bit_p5[4]), .clk(clock), .Q(positiv[4]), .Qn(negiert[4]));  // open: preset, reset
  D_Flip_Flop d_ff_6 (.D(multiplx9bit_p5[5]), .clk(clock), .Q(positiv[5]), .Qn(negiert[5]));  // open: preset, reset
  D_Flip_Flop d_ff_7 (.D(multiplx9bit_p5[6]), .clk(clock), .Q(positiv[6]), .Qn(negiert[6]));  // open: preset, reset
  D_Flip_Flop d_ff_8 (.D(multiplx9bit_p5[7]), .clk(clock), .Q(positiv[7]), .Qn(negiert[7]));  // open: preset, reset
  D_Flip_Flop d_ff_9 (.D(multiplx9bit_p5[8]), .clk(clock), .Q(positiv[8]), .Qn(negiert[8]));  // open: preset, reset
endmodule
